// Logisim project Tennis_proj.circ as structural Verilog
module main (
);

  wire button_1_out, button_2_out, clock_1_out, clock_2_out, module_display_1_game_on,
       module_display_1_reboot_out;
  wire [3:0] mem_tv_tennis_1_score1, mem_tv_tennis_1_score2;
  wire [4:0] mem_tv_tennis_1_x, mem_tv_tennis_1_y, mem_tv_tennis_1_y_r0, mem_tv_tennis_1_y_r1;
  wire [6:0] keyboard_1_data, module_display_1_clava_out;
  wire [7:0] mem_tv_tennis_1_out_5, module_display_1_out_11;
  wire [31:0] module_display_1_out_13, module_display_1_out_14, module_display_1_out_15,
       module_display_1_out_16, module_display_1_out_17, module_display_1_out_18, module_display_1_out_19,
       module_display_1_out_20, module_display_1_out_21, module_display_1_out_22, module_display_1_out_23,
       module_display_1_out_24, module_display_1_out_25, module_display_1_out_26, module_display_1_out_27,
       module_display_1_out_28, module_display_1_out_29, module_display_1_out_30, module_display_1_out_31,
       module_display_1_out_32, module_display_1_out_33, module_display_1_out_34, module_display_1_out_35,
       module_display_1_out_36, module_display_1_out_37, module_display_1_out_38, module_display_1_out_39,
       module_display_1_out_40, module_display_1_out_41, module_display_1_out_42, module_display_1_out_43,
       module_display_1_out_44, module_display_1_out_45, module_display_1_out_46, module_display_1_out_47,
       module_display_1_out_48, module_display_1_out_49, module_display_1_out_50, module_display_1_out_51,
       module_display_1_out_52, module_display_1_out_53, module_display_1_out_54, module_display_1_out_55,
       module_display_1_out_56, module_display_1_out_57, module_display_1_out_58;

  \рамка3  \u_рамка3_1  ();
  \рамка4  \u_рамка4_1  ();
  Button button_1 (.out(button_1_out));
  \рамка5  \u_рамка5_1  ();
  \рамка6  \u_рамка6_1  ();
  Button button_2 (.out(button_2_out));
  \рамка7  \u_рамка7_1  ();
  \рамка2  \u_рамка2_1  ();
  mem_TV_tennis mem_tv_tennis_1 (
    .X(mem_tv_tennis_1_x), .Y(mem_tv_tennis_1_y), .Y_r0(mem_tv_tennis_1_y_r0), .Y_r1(mem_tv_tennis_1_y_r1),
    .score1(mem_tv_tennis_1_score1), .score2(mem_tv_tennis_1_score2), .reboot(module_display_1_reboot_out),
    .clava(module_display_1_clava_out), .in_1(module_display_1_out_11), .out_5(mem_tv_tennis_1_out_5),
    .game_on(module_display_1_game_on));
  DotMatrix #(.matrixcols(7), .matrixrows(32)) dotmatrix_1 (
    .col0(module_display_1_out_13), .col1(module_display_1_out_14), .col2(module_display_1_out_15),
    .col3(module_display_1_out_16), .col4(module_display_1_out_17), .col5(module_display_1_out_18),
    .col6(module_display_1_out_19));
  DotMatrix #(.matrixcols(16), .matrixrows(32)) dotmatrix_2 (
    .col0(module_display_1_out_20), .col1(module_display_1_out_21), .col2(module_display_1_out_22),
    .col3(module_display_1_out_23), .col4(module_display_1_out_24), .col5(module_display_1_out_25),
    .col6(module_display_1_out_26), .col7(module_display_1_out_27), .col8(module_display_1_out_28),
    .col9(module_display_1_out_29), .col10(module_display_1_out_30), .col11(module_display_1_out_31),
    .col12(module_display_1_out_32), .col13(module_display_1_out_33), .col14(module_display_1_out_34),
    .col15(module_display_1_out_35));
  Module___Display module_display_1 (
    .X(mem_tv_tennis_1_x), .Y(mem_tv_tennis_1_y), .R0(mem_tv_tennis_1_y_r0), .R1(mem_tv_tennis_1_y_r1),
    .out_20(module_display_1_out_20), .out_21(module_display_1_out_21), .out_22(module_display_1_out_22),
    .out_23(module_display_1_out_23), .out_24(module_display_1_out_24), .out_25(module_display_1_out_25),
    .out_26(module_display_1_out_26), .out_27(module_display_1_out_27), .out_28(module_display_1_out_28),
    .out_29(module_display_1_out_29), .out_30(module_display_1_out_30), .out_31(module_display_1_out_31),
    .out_32(module_display_1_out_32), .out_33(module_display_1_out_33), .out_34(module_display_1_out_34),
    .out_35(module_display_1_out_35), .out_36(module_display_1_out_36), .out_37(module_display_1_out_37),
    .out_38(module_display_1_out_38), .out_39(module_display_1_out_39), .out_40(module_display_1_out_40),
    .out_41(module_display_1_out_41), .out_42(module_display_1_out_42), .out_43(module_display_1_out_43),
    .out_44(module_display_1_out_44), .out_45(module_display_1_out_45), .out_46(module_display_1_out_46),
    .out_47(module_display_1_out_47), .out_48(module_display_1_out_48), .out_49(module_display_1_out_49),
    .out_50(module_display_1_out_50), .out_51(module_display_1_out_51), .in1(mem_tv_tennis_1_score2),
    .in2(mem_tv_tennis_1_score1), .clava_out(module_display_1_clava_out),
    .reboot_out(module_display_1_reboot_out), .reboot_in(button_2_out), .clava_in(keyboard_1_data),
    .out_13(module_display_1_out_13), .out_14(module_display_1_out_14), .out_15(module_display_1_out_15),
    .out_16(module_display_1_out_16), .out_17(module_display_1_out_17), .out_18(module_display_1_out_18),
    .out_19(module_display_1_out_19), .out_52(module_display_1_out_52), .out_53(module_display_1_out_53),
    .out_54(module_display_1_out_54), .out_55(module_display_1_out_55), .out_56(module_display_1_out_56),
    .out_57(module_display_1_out_57), .out_58(module_display_1_out_58), .in_2(button_1_out),
    .in_1(mem_tv_tennis_1_out_5), .out_11(module_display_1_out_11), .game_on(module_display_1_game_on));
  \рамка8  \u_рамка8_1  ();
  Clock clock_1 (.out(clock_1_out));
  Keyboard keyboard_1 (.clk(clock_1_out), .clr(clock_2_out), .data(keyboard_1_data));  // open: re, avail
  Clock clock_2 (.out(clock_2_out));
  \рамка10  \u_рамка10_1  ();
  \рамка  \u_рамка_1  ();
  DotMatrix #(.matrixcols(16), .matrixrows(32)) dotmatrix_3 (
    .col0(module_display_1_out_36), .col1(module_display_1_out_37), .col2(module_display_1_out_38),
    .col3(module_display_1_out_39), .col4(module_display_1_out_40), .col5(module_display_1_out_41),
    .col6(module_display_1_out_42), .col7(module_display_1_out_43), .col8(module_display_1_out_44),
    .col9(module_display_1_out_45), .col10(module_display_1_out_46), .col11(module_display_1_out_47),
    .col12(module_display_1_out_48), .col13(module_display_1_out_49), .col14(module_display_1_out_50),
    .col15(module_display_1_out_51));
  \рамка9  \u_рамка9_1  ();
  DotMatrix #(.matrixcols(7), .matrixrows(32)) dotmatrix_4 (
    .col0(module_display_1_out_52), .col1(module_display_1_out_53), .col2(module_display_1_out_54),
    .col3(module_display_1_out_55), .col4(module_display_1_out_56), .col5(module_display_1_out_57),
    .col6(module_display_1_out_58));
endmodule

module part_1 (
  input  [4:0] Ball_x,
  input  [4:0] Ball_y,
  input  [4:0] R1,
  input  [4:0] R2,
  input  [4:0] ID,
  output [31:0] Data,
  output [4:0] out_7
);

  wire comparator_3_eq, rock1, rock2;
  wire [31:0] decoder_1_out0, decoder_2_out0, decoder_3_out0, multiplexer_1_out, multiplexer_2_out,
       multiplexer_3_out, or_1_out, rocket_1_bus_0_2;

  Pull_Resistor pull_resistor_1 (.node(Ball_x));
  Pull_Resistor pull_resistor_2 (.node(Ball_y));
  Pull_Resistor pull_resistor_3 (.node(R1));
  Pull_Resistor pull_resistor_4 (.node(R2));
  Pull_Resistor pull_resistor_5 (.node(ID));
  Decoder #(.select(5)) decoder_1 (
    .out0(decoder_1_out0[0]), .out1(decoder_1_out0[1]), .out2(decoder_1_out0[2]), .out3(decoder_1_out0[3]),
    .out4(decoder_1_out0[4]), .out5(decoder_1_out0[5]), .out6(decoder_1_out0[6]), .out7(decoder_1_out0[7]),
    .out8(decoder_1_out0[8]), .out9(decoder_1_out0[9]), .out10(decoder_1_out0[10]),
    .out11(decoder_1_out0[11]), .out12(decoder_1_out0[12]), .out13(decoder_1_out0[13]),
    .out14(decoder_1_out0[14]), .out15(decoder_1_out0[15]), .out16(decoder_1_out0[16]),
    .out17(decoder_1_out0[17]), .out18(decoder_1_out0[18]), .out19(decoder_1_out0[19]),
    .out20(decoder_1_out0[20]), .out21(decoder_1_out0[21]), .out22(decoder_1_out0[22]),
    .out23(decoder_1_out0[23]), .out24(decoder_1_out0[24]), .out25(decoder_1_out0[25]),
    .out26(decoder_1_out0[26]), .out27(decoder_1_out0[27]), .out28(decoder_1_out0[28]),
    .out29(decoder_1_out0[29]), .out30(decoder_1_out0[30]), .out31(decoder_1_out0[31]), .sel(Ball_y));  // open: en
  Decoder #(.select(5)) decoder_2 (
    .out0(decoder_2_out0[0]), .out1(decoder_2_out0[1]), .out2(decoder_2_out0[2]), .out3(decoder_2_out0[3]),
    .out4(decoder_2_out0[4]), .out5(decoder_2_out0[5]), .out6(decoder_2_out0[6]), .out7(decoder_2_out0[7]),
    .out8(decoder_2_out0[8]), .out9(decoder_2_out0[9]), .out10(decoder_2_out0[10]),
    .out11(decoder_2_out0[11]), .out12(decoder_2_out0[12]), .out13(decoder_2_out0[13]),
    .out14(decoder_2_out0[14]), .out15(decoder_2_out0[15]), .out16(decoder_2_out0[16]),
    .out17(decoder_2_out0[17]), .out18(decoder_2_out0[18]), .out19(decoder_2_out0[19]),
    .out20(decoder_2_out0[20]), .out21(decoder_2_out0[21]), .out22(decoder_2_out0[22]),
    .out23(decoder_2_out0[23]), .out24(decoder_2_out0[24]), .out25(decoder_2_out0[25]),
    .out26(decoder_2_out0[26]), .out27(decoder_2_out0[27]), .out28(decoder_2_out0[28]),
    .out29(decoder_2_out0[29]), .out30(decoder_2_out0[30]), .out31(decoder_2_out0[31]), .sel(R1));  // open: en
  Decoder #(.select(5)) decoder_3 (
    .out0(decoder_3_out0[0]), .out1(decoder_3_out0[1]), .out2(decoder_3_out0[2]), .out3(decoder_3_out0[3]),
    .out4(decoder_3_out0[4]), .out5(decoder_3_out0[5]), .out6(decoder_3_out0[6]), .out7(decoder_3_out0[7]),
    .out8(decoder_3_out0[8]), .out9(decoder_3_out0[9]), .out10(decoder_3_out0[10]),
    .out11(decoder_3_out0[11]), .out12(decoder_3_out0[12]), .out13(decoder_3_out0[13]),
    .out14(decoder_3_out0[14]), .out15(decoder_3_out0[15]), .out16(decoder_3_out0[16]),
    .out17(decoder_3_out0[17]), .out18(decoder_3_out0[18]), .out19(decoder_3_out0[19]),
    .out20(decoder_3_out0[20]), .out21(decoder_3_out0[21]), .out22(decoder_3_out0[22]),
    .out23(decoder_3_out0[23]), .out24(decoder_3_out0[24]), .out25(decoder_3_out0[25]),
    .out26(decoder_3_out0[26]), .out27(decoder_3_out0[27]), .out28(decoder_3_out0[28]),
    .out29(decoder_3_out0[29]), .out30(decoder_3_out0[30]), .out31(decoder_3_out0[31]), .sel(R2));  // open: en
  Comparator #(.width(5)) comparator_1 (.a(5'b00100), .b(ID), .eq(rock1));  // open: gt, lt
  Comparator #(.width(5)) comparator_2 (.a(ID), .b(5'b11011), .eq(rock2));  // open: gt, lt
  Multiplexer #(.width(32)) multiplexer_1 (
    .in0({32{1'b0}}), .in1(decoder_2_out0), .out(multiplexer_1_out), .sel(rock1));  // open: en
  Multiplexer #(.width(32)) multiplexer_2 (
    .in0({32{1'b0}}), .in1(decoder_3_out0), .out(multiplexer_2_out), .sel(rock2));  // open: en
  Comparator #(.width(5)) comparator_3 (.a(Ball_x), .b(ID), .eq(comparator_3_eq));  // open: gt, lt
  assign or_1_out = multiplexer_1_out | multiplexer_2_out;  // OR_Gate or_1, 32 bits wide
  rocket rocket_1 (.bus_0(or_1_out), .bus_0_2(rocket_1_bus_0_2));
  Adder #(.width(5)) adder_1 (.a(ID), .b(5'b00001), .out(out_7));  // open: cin, cout
  Multiplexer #(.width(32)) multiplexer_3 (
    .in0({32{1'b0}}), .in1(decoder_1_out0), .out(multiplexer_3_out), .sel(comparator_3_eq));  // open: en
  assign Data = multiplexer_3_out | rocket_1_bus_0_2;  // OR_Gate or_2, 32 bits wide

  // Other names for the same wires on the sheet: Rocket_1[4:0] = R1; Rocket_2[4:0] = R2
endmodule

module rocket (
  input  [31:0] bus_0,
  output [31:0] bus_0_2
);

  wire [31:0] shifter_1_out, shifter_2_out;

  Shifter #(.width(32)) shifter_1 (.in(bus_0), .\dist (5'b00001), .out(shifter_1_out));
  Shifter #(.width(32), .shift("lr")) shifter_2 (.in(bus_0), .\dist (5'b00001), .out(shifter_2_out));
  assign bus_0_2 = shifter_1_out | bus_0 | shifter_2_out;  // OR_Gate or_1, 32 bits wide
endmodule

module part_2 (
  input  [4:0] BX,
  input  [4:0] BY,
  input  [4:0] R1,
  input  [4:0] R2,
  input  [4:0] ID,
  output [31:0] data,
  output [31:0] data_2,
  output [31:0] data_3,
  output [31:0] data_4,
  output [31:0] data_5,
  output [31:0] data_6,
  output [31:0] data_7,
  output [31:0] data_8,
  output [4:0] BX_2,
  output [4:0] BY_2,
  output [4:0] R1_2,
  output [4:0] R2_2,
  output [4:0] ID_2
);

  wire [4:0] part_1_1_out_7, part_1_2_out_7, part_1_3_out_7, part_1_4_out_7, part_1_5_out_7, part_1_6_out_7,
       part_1_7_out_7;

  part_1 part_1_1 (.Ball_x(BX), .Ball_y(BY), .R1(R1), .R2(R2), .ID(ID), .Data(data), .out_7(part_1_1_out_7));
  part_1 part_1_2 (
    .Ball_x(BX), .Ball_y(BY), .R1(R1), .R2(R2), .ID(part_1_1_out_7), .Data(data_2), .out_7(part_1_2_out_7));
  part_1 part_1_3 (
    .Ball_x(BX), .Ball_y(BY), .R1(R1), .R2(R2), .ID(part_1_2_out_7), .Data(data_3), .out_7(part_1_3_out_7));
  part_1 part_1_4 (
    .Ball_x(BX), .Ball_y(BY), .R1(R1), .R2(R2), .ID(part_1_3_out_7), .Data(data_4), .out_7(part_1_4_out_7));
  part_1 part_1_5 (
    .Ball_x(BX), .Ball_y(BY), .R1(R1), .R2(R2), .ID(part_1_4_out_7), .Data(data_5), .out_7(part_1_5_out_7));
  part_1 part_1_6 (
    .Ball_x(BX), .Ball_y(BY), .R1(R1), .R2(R2), .ID(part_1_5_out_7), .Data(data_6), .out_7(part_1_6_out_7));
  part_1 part_1_7 (
    .Ball_x(BX), .Ball_y(BY), .R1(R1), .R2(R2), .ID(part_1_6_out_7), .Data(data_7), .out_7(part_1_7_out_7));
  part_1 part_1_8 (.Ball_x(BX), .Ball_y(BY), .R1(R1), .R2(R2), .ID(part_1_7_out_7), .Data(data_8), .out_7(ID_2));

  assign BX_2 = BX;
  assign BY_2 = BY;
  assign R1_2 = R1;
  assign R2_2 = R2;
endmodule

module counter (
  input  [4:0] ball_x,
  input  restart,
  output [3:0] r0,
  output [3:0] r1
);

  wire buffer_1_out, comparator_1_eq, comparator_2_eq;

  buf buffer_1 (buffer_1_out, restart);
  Comparator #(.width(5)) comparator_1 (.a(ball_x), .b({5{1'b1}}), .eq(comparator_1_eq));  // open: gt, lt
  Counter #(.width(4), .max('h9)) counter_1 (
    .Q(r0), .clk(comparator_2_eq), .clr(buffer_1_out));  // open: load, D, count, carry
  Comparator #(.width(5)) comparator_2 (.a(ball_x), .b({5{1'b0}}), .eq(comparator_2_eq));  // open: gt, lt
  Counter #(.width(4), .max('h9)) counter_2 (
    .Q(r1), .clk(comparator_1_eq), .clr(buffer_1_out));  // open: load, D, count, carry
endmodule

// ASCII
module clava (
  input  [6:0] data,
  output [4:0] _5_data_out
);

  wire clock_1_out, comparator_1_eq, comparator_1_gt, comparator_2_eq, comparator_2_lt, comparator_3_eq,
       comparator_4_eq, comparator_5_eq, or_1_out, or_2_out;
  wire [1:0] priority_encoder_1_out;
  wire [4:0] adder_1_out, multiplexer_1_out, multiplexer_2_out, register_1_q, subtractor_1_out;

  Register #(.width(5)) register_1 (.D(_5_data_out), .Q(register_1_q), .clk(clock_1_out));  // open: en, clr
  Clock clock_1 (.out(clock_1_out));
  // Probe on data
  Multiplexer #(.width(5), .enable("false")) multiplexer_1 (
    .in0(register_1_q), .in1(5'b11110), .out(multiplexer_1_out), .sel(or_1_out));
  or or_1 (or_1_out, comparator_1_gt, comparator_1_eq);
  Comparator #(.width(5), .mode("unsigned")) comparator_1 (
    .a(register_1_q), .b(5'b11110), .gt(comparator_1_gt), .eq(comparator_1_eq));  // open: lt
  Comparator #(.width(5), .mode("unsigned")) comparator_2 (
    .a(register_1_q), .b(5'b00001), .eq(comparator_2_eq), .lt(comparator_2_lt));  // open: gt
  or or_2 (or_2_out, comparator_2_eq, comparator_2_lt);
  Comparator #(.width(7)) comparator_3 (.a(data), .b(7'b1110111), .eq(comparator_3_eq));  // open: gt, lt
  Comparator #(.width(7)) comparator_4 (.a(data), .b(7'b1110011), .eq(comparator_4_eq));  // open: gt, lt
  Comparator #(.width(7)) comparator_5 (.a(data), .b(7'b0100000), .eq(comparator_5_eq));  // open: gt, lt
  Multiplexer #(.width(5), .enable("false")) multiplexer_2 (
    .in0(multiplexer_1_out), .in1(5'b00001), .out(multiplexer_2_out), .sel(or_2_out));
  // Probe on priority_encoder_1_out
  Priority_Encoder #(.select(2)) priority_encoder_1 (
    .in0(1'b1), .in1(comparator_3_eq), .in2(comparator_4_eq), .in3(comparator_5_eq),
    .out(priority_encoder_1_out));  // open: gs, en_out, en_in
  Adder #(.width(5)) adder_1 (.a(multiplexer_2_out), .b(5'b00001), .out(adder_1_out));  // open: cin, cout
  Subtractor #(.width(5)) subtractor_1 (
    .a(multiplexer_2_out), .b(5'b00001), .out(subtractor_1_out));  // open: bin, bout
  Multiplexer #(.select(2), .width(5), .enable("false")) multiplexer_3 (
    .in0(multiplexer_2_out), .in1(adder_1_out), .in2(subtractor_1_out), .in3(5'b10000), .out(_5_data_out),
    .sel(priority_encoder_1_out));

  // Other names for the same wires on the sheet: data_in[4:0] = _5_data_out
endmodule

module \модуль  (
  input  [7:0] in_1,
  output [7:0] out_2
);

  wire [7:0] adder_1_out, not_1_out;

  assign not_1_out = ~in_1;  // NOT_Gate not_1, 8 bits wide
  Adder adder_1 (.a(not_1_out), .b(8'h1), .out(adder_1_out));  // open: cin, cout
  Multiplexer #(.width(8)) multiplexer_1 (.in0(in_1), .in1(adder_1_out), .out(out_2), .sel(in_1[7]));  // open: en
endmodule

module bot (
  input  [7:0] y,
  input  [7:0] x,
  input  [7:0] dy,
  input  [7:0] dx,
  input  sig,
  input  reboot,
  input  [7:0] errorx,
  input  [7:0] errory,
  output sign,
  output [7:0] y_r1
);

  wire and_1_out, and_2_out, and_4_out, clk, comparator_1_eq, comparator_2_eq, comparator_3_eq,
       comparator_4_gt, comparator_5_gt, comparator_6_eq, comparator_6_gt, comparator_7_eq, comparator_7_gt,
       comparator_8_eq, comparator_9_eq, comparator_10_eq, comparator_10_gt, comparator_11_eq, high_low,
       or_1_out, or_2_out, win;
  wire [2:0] win_out;
  wire [7:0] adder_1_out, buffer_1_out, controlled_buffer_1_out, controlled_buffer_2_out,
       controlled_buffer_3_out, controlled_buffer_4_out, delx, divider_1_out, dx_t, dy_t, incdec_1_out,
       incdec_2_out, incdec_3_out, incdec_4_out, incdec_5_out, incdec_6_out, incdec_7_out, multiplexer_1_out,
       multiplexer_4_out, multiplexer_5_out, multiplexer_6_out, multiplier_1_out, multiplier_2_out,
       neg_1_out, register_1_q, register_2_q, register_3_q, ring_1_out_2, sig_t, subtractor_1_out;

  Clock clock_1 (.out(clk));
  Pull_Resistor pull_resistor_1 (.node(y));
  Comparator comparator_1 (.a(8'h2), .b(delx), .eq(comparator_1_eq));  // open: gt, lt
  Comparator comparator_2 (.a(x), .b(8'h6), .eq(comparator_2_eq));  // open: gt, lt
  Pull_Resistor pull_resistor_2 (.node(x));
  assign controlled_buffer_1_out = and_1_out ? dy_t : 8'bz;  // Controlled_Buffer controlled_buffer_1
  assign controlled_buffer_2_out = and_1_out ? dx_t : 8'bz;  // Controlled_Buffer controlled_buffer_2
  assign controlled_buffer_3_out = and_1_out ? x : 8'bz;  // Controlled_Buffer controlled_buffer_3
  and and_1 (and_1_out, comparator_1_eq, sig, comparator_2_eq);
  Pull_Resistor pull_resistor_3 (.node(controlled_buffer_1_out));
  Pull_Resistor pull_resistor_4 (.node(controlled_buffer_2_out));
  Pull_Resistor pull_resistor_5 (.node(controlled_buffer_3_out));
  assign controlled_buffer_4_out = and_1_out ? y : 8'bz;  // Controlled_Buffer controlled_buffer_4
  Pull_Resistor pull_resistor_6 (.node(controlled_buffer_4_out));
  Random #(.width(3)) u_win (.clk(and_1_out), .next(and_1_out), .out(win_out));  // open: clr
  Random #(.width(1)) win_2 (.clk(and_1_out), .next(and_1_out), .out(high_low));  // open: clr
  Pull_Resistor pull_resistor_7 (.node(dy));
  Multiplier multiplier_1 (
    .a(controlled_buffer_1_out), .b(subtractor_1_out), .out(multiplier_1_out));  // open: cin, cout
  Subtractor subtractor_1 (.a(8'h1a), .b(controlled_buffer_3_out), .out(subtractor_1_out));  // open: bin, bout
  Comparator #(.width(3)) comparator_3 (.a(3'b110), .b(win_out), .eq(comparator_3_eq));  // open: gt, lt
  Comparator comparator_4 (.a(errorx), .b(8'h2), .gt(comparator_4_gt));  // open: eq, lt
  Multiplexer #(.width(8)) multiplexer_1 (
    .in0(errory), .in1(8'h2), .out(multiplexer_1_out), .sel(comparator_4_gt));  // open: en
  Multiplier multiplier_2 (
    .a(controlled_buffer_2_out), .b(controlled_buffer_4_out), .out(multiplier_2_out));  // open: cin, cout
  not not_1 (win, comparator_3_eq);
  Comparator comparator_5 (.a(errory), .b(8'h2), .gt(comparator_5_gt));  // open: eq, lt
  Multiplexer #(.width(8)) multiplexer_2 (.in0(errorx), .in1(8'h2), .out(dx_t), .sel(comparator_5_gt));  // open: en
  Pull_Resistor pull_resistor_8 (.node(dx));
  Adder adder_1 (.a(multiplier_1_out), .b(multiplier_2_out), .out(adder_1_out));  // open: cin, cout
  Multiplexer #(.width(8)) multiplexer_3 (
    .in0(multiplexer_1_out), .in1(neg_1_out), .out(dy_t), .sel(dy[7]));  // open: en
  neg neg_1 (.in(multiplexer_1_out), .out(neg_1_out));
  Multiplier multiplier_3 (.a(8'h2), .b(dx), .out(delx));  // open: cin, cout
  // Probe on divider_1_out
  Divider divider_1 (.a(adder_1_out), .b(controlled_buffer_2_out), .out(divider_1_out));  // open: upper, rem
  ring ring_1 (.in_1(divider_1_out), .out_2(ring_1_out_2));
  Register register_1 (.D(ring_1_out_2), .en(and_1_out), .Q(register_1_q), .clk(clk), .clr(reboot));
  incdec incdec_1 (.in(y_r1), .out(incdec_1_out), .up_down(1'b1));
  incdec incdec_2 (.in(y_r1), .out(incdec_2_out), .up_down(1'b0));
  incdec incdec_3 (.in(register_1_q), .out(incdec_3_out), .up_down(high_low));
  incdec incdec_4 (.in(incdec_3_out), .out(incdec_4_out), .up_down(high_low));
  incdec incdec_5 (.in(incdec_4_out), .out(incdec_5_out), .up_down(high_low));
  Comparator comparator_6 (.a(incdec_1_out), .b(y), .gt(comparator_6_gt), .eq(comparator_6_eq));  // open: lt
  Comparator comparator_7 (.a(y), .b(incdec_2_out), .gt(comparator_7_gt), .eq(comparator_7_eq));  // open: lt
  Register register_2 (.D(incdec_5_out), .Q(register_2_q), .clk(clk));  // open: en, clr
  or or_1 (or_1_out, comparator_6_gt, comparator_6_eq);
  or or_2 (or_2_out, comparator_7_gt, comparator_7_eq);
  Comparator comparator_8 (.a(8'h2), .b(delx), .eq(comparator_8_eq));  // open: gt, lt
  Comparator comparator_9 (.a(8'h1a), .b(x), .eq(comparator_9_eq));  // open: gt, lt
  Multiplexer #(.width(8), .disabled(0)) multiplexer_4 (
    .in0(register_2_q), .in1(register_1_q), .out(multiplexer_4_out), .sel(win));  // open: en
  and and_2 (and_2_out, or_1_out, or_2_out);
  and and_3 (sign, and_2_out, comparator_8_eq, comparator_9_eq);
  incdec incdec_6 (.in(register_3_q), .out(incdec_6_out), .up_down(comparator_10_gt));
  Comparator comparator_10 (
    .a(multiplexer_4_out), .b(register_3_q), .gt(comparator_10_gt), .eq(comparator_10_eq));  // open: lt
  and and_4 (and_4_out, sig, comparator_11_eq);
  Comparator comparator_11 (.a(8'h2), .b(delx), .eq(comparator_11_eq));  // open: gt, lt
  Multiplexer #(.width(8)) multiplexer_5 (
    .in0(incdec_6_out), .in1(multiplexer_4_out), .out(multiplexer_5_out), .sel(comparator_10_eq));  // open: en
  Register register_3 (.D(multiplexer_5_out), .en(and_4_out), .Q(register_3_q), .clk(clk), .clr(reboot));
  assign buffer_1_out = register_3_q;  // Buffer buffer_1, 8 bits wide
  Multiplexer #(.width(8)) multiplexer_6 (
    .in0({8{1'b0}}), .in1(8'h1), .out(multiplexer_6_out), .sel(sign));  // open: en
  assign sig_t = multiplexer_6_out;  // Buffer buffer_2, 8 bits wide
  incdec incdec_7 (.in(buffer_1_out), .out(incdec_7_out), .up_down(1'b0));
  Norm_cord norm_cord_1 (.in_1(incdec_7_out), .out_2(y_r1));

  // Other names for the same wires on the sheet: clr = reboot; dely[7:0] = dy
endmodule

module ring (
  input  [7:0] in_1,
  output [7:0] out_2
);

  wire [7:0] divider_1_out, divider_1_rem, subtractor_1_out;

  // Probe on in_1
  Divider divider_1 (.a(in_1), .b(8'h20), .out(divider_1_out), .rem(divider_1_rem));  // open: upper
  Subtractor subtractor_1 (.a(8'h20), .b(divider_1_rem), .out(subtractor_1_out));  // open: bin, bout
  Multiplexer #(.width(8)) multiplexer_1 (
    .in0(divider_1_rem), .in1(subtractor_1_out), .out(out_2), .sel(divider_1_out[0]));  // open: en
endmodule

module intel_core (
  input  game_on_off,
  input  clr,
  input  [4:0] Y_r0,
  output [4:0] Y_ball,
  output [4:0] X_Ball,
  output [4:0] Y_r1
);

  wire A1, A2, A3, A4, A5, A6, A7, A8, A9, A10, A11, A11_prime, alpha0_1_sign_2, and_1_out, bot_1_sign,
       cdm_8_mark5_1_data_inst, cdm_8_mark5_1_mem_cycle, clk, clock_1_out, clock_2_out, code,
       comparator_1_lt, comparator_2_lt, comparator_3_eq, comparator_4_eq, comparator_5_gt, comparator_6_eq,
       data, decoder_3_out4, decoder_3_out5, decoder_3_out6, decoder_3_out7, decoder_3_out8, decoder_3_out9,
       decoder_3_out10, I_O_rw, I_O_sel, nand_1_out, not_1_out, not_2_out, not_3_out, not_4_out, not_5_out,
       not_6_out, or_1_out, r, RAM, vec_adr, w;
  wire [7:0] addr, alpha0_1_x_max, alpha0_1_y_max, bot_1_y_r1, cdm_8_mark5_1_data_out, cdm_8_mark5_1_pc,
       cdm_8_mark5_1_ps, cdm_8_mark5_1_r0, cdm_8_mark5_1_r1, cdm_8_mark5_1_r2, cdm_8_mark5_1_r3,
       cdm_8_mark5_1_sp, controlled_buffer_3_out, dat, demultiplexer_1_out0, demultiplexer_1_out1,
       demultiplexer_1_out2, demultiplexer_1_out3, demultiplexer_1_out6, dx, dy, incdec_1_out, incdec_2_out,
       multiplexer_1_out, multiplexer_2_out, multiplexer_3_out, n5_to_8_bit_1_out_2, sign, signum, x, x_max,
       y, y_max, y_r0_new, y_r0_old, y_r1_t;

  Multiplexer #(.width(8)) multiplexer_1 (
    .in0(x_max), .in1(y_max), .out(multiplexer_1_out), .sel(signum[0]));  // open: en
  incdec incdec_1 (.in(y_r0_new), .out(incdec_1_out), .up_down(1'b1));
  incdec incdec_2 (.in(y_r0_new), .out(incdec_2_out), .up_down(1'b0));
  Clock clock_1 (.out(clock_1_out));
  assign clk = game_on_off ? clock_1_out : 1'bz;  // Controlled_Buffer controlled_buffer_1
  alpha0 alpha0_1 (
    .\new (y_r0_new), .old(y_r0_old), .v_0(multiplexer_1_out), .sign(vec_adr), .y_max(alpha0_1_y_max),
    .x_max(alpha0_1_x_max), .sign_2(alpha0_1_sign_2));
  Comparator comparator_1 (.a(incdec_1_out), .b(y), .lt(comparator_1_lt));  // open: gt, eq
  Comparator comparator_2 (.a(y), .b(incdec_2_out), .lt(comparator_2_lt));  // open: gt, eq
  Comparator comparator_3 (.a({8{1'b1}}), .b(dx), .eq(comparator_3_eq));  // open: gt, lt
  Comparator comparator_4 (.a(8'h5), .b(x), .eq(comparator_4_eq));  // open: gt, lt
  // Probe on cdm_8_mark5_1_r1
  // Probe on cdm_8_mark5_1_r3
  // Probe on cdm_8_mark5_1_r0
  // Probe on cdm_8_mark5_1_r2
  Multiplexer #(.width(8)) multiplexer_2 (
    .in0({8{1'b0}}), .in1(8'h1), .out(multiplexer_2_out), .sel(alpha0_1_sign_2), .en(vec_adr));
  // Probe on cdm_8_mark5_1_ps
  // Probe on cdm_8_mark5_1_sp
  // Probe on cdm_8_mark5_1_pc
  CdM_8_mark5 cdm_8_mark5_1 (
    .clock(clk), .addr(addr), .mem_read(I_O_rw), .mem_cycle(cdm_8_mark5_1_mem_cycle),
    .data_inst(cdm_8_mark5_1_data_inst), .data_out(cdm_8_mark5_1_data_out),
    .data_in(controlled_buffer_3_out), .r0(cdm_8_mark5_1_r0), .r1(cdm_8_mark5_1_r1), .r2(cdm_8_mark5_1_r2),
    .r3(cdm_8_mark5_1_r3), .PC(cdm_8_mark5_1_pc), .SP(cdm_8_mark5_1_sp), .PS(cdm_8_mark5_1_ps), .clr(clr));  // open: IAck, IRQ, vec
  _5_to_8_bit u_5_to_8_bit_1 (.in_1(Y_r0), .out_2(n5_to_8_bit_1_out_2));
  bot bot_1 (
    .sig(A11), .sign(bot_1_sign), .y_r1(bot_1_y_r1), .y(y), .x(x), .dy(dy), .dx(dx), .errorx(x_max),
    .reboot(clr), .errory(y_max));
  and and_1 (and_1_out, ~comparator_1_lt, ~comparator_2_lt);  // AND_Gate
  and and_2 (vec_adr, and_1_out, comparator_3_eq, comparator_4_eq);
  // Probe on addr
  Decoder #(.disabled(0)) decoder_1 (
    .out0(code), .out1(data), .sel(cdm_8_mark5_1_data_inst), .en(cdm_8_mark5_1_mem_cycle));
  not not_1 (not_1_out, I_O_rw);
  assign dat = not_1_out ? cdm_8_mark5_1_data_out : 8'bz;  // Controlled_Buffer controlled_buffer_2
  assign controlled_buffer_3_out = I_O_rw ? dat : 8'bz;  // Controlled_Buffer controlled_buffer_3
  Demultiplexer #(.select(4), .width(8), .tristate("true")) demultiplexer_1 (
    .out0(demultiplexer_1_out0), .out1(demultiplexer_1_out1), .out2(demultiplexer_1_out2),
    .out3(demultiplexer_1_out3), .out4(n5_to_8_bit_1_out_2), .out5(n5_to_8_bit_1_out_2),
    .out6(demultiplexer_1_out6), .out7(bot_1_y_r1), .out8(alpha0_1_y_max), .out9(alpha0_1_x_max),
    .out10(multiplexer_2_out), .in(dat), .sel(addr[3:0]), .en(r));  // open: out11, out12, out13, out14, out15
  // Probe on dat
  RAM ram_1 (.addr(addr), .data(dat), .sel(RAM), .clk(clk), .ld(I_O_rw), .clr(clr));
  ROM rom_1 (.addr(addr), .data(dat), .sel(code));
  Multiplexer #(.width(8)) multiplexer_3 (
    .in0({8{1'b0}}), .in1(8'h1), .out(multiplexer_3_out), .sel(or_1_out));  // open: en
  or or_1 (or_1_out, bot_1_sign, vec_adr);
  assign demultiplexer_1_out6 = multiplexer_3_out;  // Buffer buffer_1, 8 bits wide
  and and_3 (I_O_sel, not_6_out, data);
  not not_2 (not_2_out, not_3_out);
  not not_3 (not_3_out, not_4_out);
  not not_4 (not_4_out, not_5_out);
  not not_5 (not_5_out, clk);
  not not_6 (not_6_out, nand_1_out);
  and and_4 (RAM, nand_1_out, data);
  nand nand_1 (nand_1_out, comparator_5_gt, addr[4], addr[6], addr[7]);
  Store store_1 (
    .in_12(demultiplexer_1_out0), .in_13(demultiplexer_1_out1), .in_14(demultiplexer_1_out2),
    .in_15(demultiplexer_1_out3), .in_16(n5_to_8_bit_1_out_2), .in_17(n5_to_8_bit_1_out_2),
    .in_18(demultiplexer_1_out6), .in_19(bot_1_y_r1), .out_25(y), .out_26(x), .out_27(dy), .out_28(dx),
    .out_29(y_r0_new), .out_30(y_r0_old), .out_31(sign), .in_1(A1), .in_2(A2), .in_3(A3), .in_4(A4),
    .in_5(A5), .in_6(A6), .in_7(A7), .in_8(A8), .clk(not_2_out), .out_32(y_r1_t), .clr(clr),
    .in_20(alpha0_1_y_max), .out_33(y_max), .in_21(alpha0_1_x_max), .out_34(x_max), .in_9(A9), .in_10(A10),
    .in_22(multiplexer_2_out), .out_35(signum), .in_11(A11_prime));
  Comparator #(.width(4), .mode("unsigned")) comparator_5 (
    .a(4'b1011), .b(addr[3:0]), .gt(comparator_5_gt));  // open: eq, lt
  Multiplexer #(.select(4), .width(8)) multiplexer_4 (
    .in0(y), .in1(x), .in2(dy), .in3(dx), .in4(y_r0_new), .in5(y_r0_old), .in6(sign), .in7(y_r1_t),
    .in8(y_max), .in9(x_max), .in10(signum), .out(dat), .sel(addr[3:0]), .en(w));  // open: in11, in12, in13, in14, in15
  or or_2 (A5, decoder_3_out4, clk);
  or or_3 (A6, decoder_3_out5, clock_2_out);
  Clock #(.lowDuration(500)) clock_2 (.out(clock_2_out));
  or or_4 (A7, decoder_3_out6, clk);
  or or_5 (A8, decoder_3_out7, clk);
  or or_6 (A9, decoder_3_out8, vec_adr);
  or or_7 (A10, decoder_3_out9, vec_adr);
  Pull_Resistor pull_resistor_1 (.node(r));
  Pull_Resistor pull_resistor_2 (.node(w));
  Comparator #(.width(4)) comparator_6 (.a(addr[3:0]), .b(4'b1010), .eq(comparator_6_eq));  // open: gt, lt
  Decoder decoder_2 (.out0(r), .out1(w), .sel(I_O_rw), .en(I_O_sel));
  or or_8 (A11_prime, decoder_3_out10, vec_adr, A11);
  and and_5 (A11, comparator_6_eq, w);
  Decoder #(.select(4), .disabled(0)) decoder_3 (
    .out0(A1), .out1(A2), .out2(A3), .out3(A4), .out4(decoder_3_out4), .out5(decoder_3_out5),
    .out6(decoder_3_out6), .out7(decoder_3_out7), .out8(decoder_3_out8), .out9(decoder_3_out9),
    .out10(decoder_3_out10), .sel(addr[3:0]), .en(r));  // open: out11, out12, out13, out14, out15
  _8_to_5_bit u_8_to_5_bit_1 (.in_1(y), .out_2(Y_ball));
  _8_to_5_bit u_8_to_5_bit_2 (.in_1(x), .out_2(X_Ball));
  _8_to_5_bit u_8_to_5_bit_3 (.in_1(y_r1_t), .out_2(Y_r1));

  // Other names for the same wires on the sheet: I_O_addr[3:0] = addr[3:0]; I_O_data[7:0] = dat; rw = I_O_rw;
  //   select = I_O_sel

  // Notes on the sheet:
  //   contents of rom_1 (hex, n*v repeats v):
  //   d0 ef d1 0 a1 d0 ee d1 0 a1 d0 f2 d1 1 a1 d0 f3 d1 ff a1 d0 f0 d1 a a1 d0 f1 d1 14 a1 d0 f7 d1 f a1
  //   d0 f8 d1 2 a1 d0 f9 d1 2 a1 d0 fa d1 1 a1 d6 64 d1 1f d2 0 d0 f0 b0 71 e1 45 d0 f2 d3 ff a3 ee 4d 72
  //   e1 4d d0 f2 d3 1 a3 d0 f1 b0 71 e1 5a d0 f3 d3 ff a3 ee 62 72 e1 62 d0 f3 d3 1 a3 d6 64 c4 d2 1 d3
  //   f6 bf 7e e1 72 d0 f3 b1 85 a1 d0 fa b0 d1 1 71 e1 9d d0 2 d3 ef bd 11 ad bd 74 e4 93 d0 f3 b0 d1 f1
  //   b6 12 a6 bd d2 f8 ba 36 ae d3 f0 bd d0 f2 b0 11 ad ee be d0 2 d3 ee bd 11 ad bd 74 e4 b6 d0 f2 b0 d1
  //   f0 b6 12 a6 bd d2 f9 ba 36 ae d3 f1 bd d0 f3 b0 11 ad ee 34
  //   read
  //   write
endmodule

module _8_to_5_bit (
  input  [7:0] in_1,
  output [4:0] out_2
);


  assign out_2 = in_1[4:0];
endmodule

// 2
module Store (
  input  in_1,
  input  in_2,
  input  in_3,
  input  in_4,
  input  in_5,
  input  in_6,
  input  in_7,
  input  in_8,
  input  in_9,
  input  in_10,
  input  in_11,
  input  [7:0] in_12,
  input  [7:0] in_13,
  input  [7:0] in_14,
  input  [7:0] in_15,
  input  [7:0] in_16,
  input  [7:0] in_17,
  input  [7:0] in_18,
  input  [7:0] in_19,
  input  [7:0] in_20,
  input  [7:0] in_21,
  input  [7:0] in_22,
  input  clr,
  input  clk,
  output [7:0] out_25,
  output [7:0] out_26,
  output [7:0] out_27,
  output [7:0] out_28,
  output [7:0] out_29,
  output [7:0] out_30,
  output [7:0] out_31,
  output [7:0] out_32,
  output [7:0] out_33,
  output [7:0] out_34,
  output [7:0] out_35
);

  Register register_1 (.D(in_12), .en(in_1), .Q(out_25), .clk(clk), .clr(clr));
  Register register_2 (.D(in_13), .en(in_2), .Q(out_26), .clk(clk), .clr(clr));
  Register register_3 (.D(in_14), .en(in_3), .Q(out_27), .clk(clk), .clr(clr));
  Register register_4 (.D(in_15), .en(in_4), .Q(out_28), .clk(clk), .clr(clr));
  Register register_5 (.D(in_16), .en(in_5), .Q(out_29), .clk(clk), .clr(clr));
  Register register_6 (.D(in_17), .en(in_6), .Q(out_30), .clk(clk), .clr(clr));
  Register register_7 (.D(in_18), .en(in_7), .Q(out_31), .clk(clk), .clr(clr));
  Register register_8 (.D(in_19), .en(in_8), .Q(out_32), .clk(clk), .clr(clr));
  Register register_9 (.D(in_20), .en(in_9), .Q(out_33), .clk(clk), .clr(clr));
  Register register_10 (.D(in_21), .en(in_10), .Q(out_34), .clk(clk), .clr(clr));
  Register register_11 (.D(in_22), .en(in_11), .Q(out_35), .clk(clk), .clr(clr));
endmodule

module neg (
  input  [7:0] in,
  output [7:0] out
);

  wire [7:0] not_1_out;

  Pull_Resistor pull_resistor_1 (.node(in));
  assign not_1_out = ~in;  // NOT_Gate not_1, 8 bits wide
  Adder adder_1 (.a(not_1_out), .b(8'h1), .out(out));  // open: cin, cout
endmodule

module Module___Display (
  input  [7:0] in_1,
  input  in_2,
  input  [4:0] X,
  input  [4:0] Y,
  input  [4:0] R0,
  input  [4:0] R1,
  input  [3:0] in1,
  input  [3:0] in2,
  input  reboot_in,
  input  [6:0] clava_in,
  output [7:0] out_11,
  output game_on,
  output [31:0] out_13,
  output [31:0] out_14,
  output [31:0] out_15,
  output [31:0] out_16,
  output [31:0] out_17,
  output [31:0] out_18,
  output [31:0] out_19,
  output [31:0] out_20,
  output [31:0] out_21,
  output [31:0] out_22,
  output [31:0] out_23,
  output [31:0] out_24,
  output [31:0] out_25,
  output [31:0] out_26,
  output [31:0] out_27,
  output [31:0] out_28,
  output [31:0] out_29,
  output [31:0] out_30,
  output [31:0] out_31,
  output [31:0] out_32,
  output [31:0] out_33,
  output [31:0] out_34,
  output [31:0] out_35,
  output [31:0] out_36,
  output [31:0] out_37,
  output [31:0] out_38,
  output [31:0] out_39,
  output [31:0] out_40,
  output [31:0] out_41,
  output [31:0] out_42,
  output [31:0] out_43,
  output [31:0] out_44,
  output [31:0] out_45,
  output [31:0] out_46,
  output [31:0] out_47,
  output [31:0] out_48,
  output [31:0] out_49,
  output [31:0] out_50,
  output [31:0] out_51,
  output [31:0] out_52,
  output [31:0] out_53,
  output [31:0] out_54,
  output [31:0] out_55,
  output [31:0] out_56,
  output [31:0] out_57,
  output [31:0] out_58,
  output [6:0] clava_out,
  output reboot_out
);

  wire and_1_out, comparator_1_eq, comparator_2_eq, comparator_3_eq, or_2_out;
  wire [4:0] part_2_1_bx_2, part_2_1_by_2, part_2_1_id_2, part_2_1_r1_2, part_2_1_r2_2, part_2_2_bx_2,
       part_2_2_by_2, part_2_2_id_2, part_2_2_r1_2, part_2_2_r2_2, part_2_3_bx_2, part_2_3_by_2,
       part_2_3_id_2, part_2_3_r1_2, part_2_3_r2_2;
  wire [6:0] digit_on_5_7_1_out_2, digit_on_5_7_1_out_3, digit_on_5_7_1_out_4, digit_on_5_7_1_out_5,
       digit_on_5_7_1_out_6, digit_on_5_7_2_out_2, digit_on_5_7_2_out_3, digit_on_5_7_2_out_4,
       digit_on_5_7_2_out_5, digit_on_5_7_2_out_6;
  wire [31:0] panel_1_out_2, panel_2_out_2, panel_3_out_2, panel_4_out_2, panel_5_out_2, panel_6_out_2,
       panel_7_out_2, panel_8_out_2, panel_9_out_2, panel_10_out_2, part_2_1_data, part_2_1_data_2,
       part_2_1_data_3, part_2_1_data_4, part_2_1_data_5, part_2_1_data_6, part_2_1_data_7, part_2_1_data_8,
       part_2_2_data, part_2_2_data_2, part_2_2_data_3, part_2_2_data_4, part_2_2_data_5, part_2_2_data_6,
       part_2_2_data_7, part_2_2_data_8, part_2_3_data, part_2_3_data_2, part_2_3_data_3, part_2_3_data_4,
       part_2_3_data_5, part_2_3_data_6, part_2_3_data_7, part_2_3_data_8, part_2_4_data, part_2_4_data_2,
       part_2_4_data_3, part_2_4_data_4, part_2_4_data_5, part_2_4_data_6, part_2_4_data_7, part_2_4_data_8;

  Comparator comparator_1 (.a(in_1), .b({8{1'b1}}), .eq(comparator_1_eq));  // open: gt, lt
  Pull_Resistor pull_resistor_1 (.node(comparator_1_eq));
  and and_1 (and_1_out, comparator_1_eq, in_2);
  or or_1 (reboot_out, and_1_out, or_2_out, reboot_in);
  Comparator #(.width(4)) comparator_2 (.a(in1), .b(4'b1001), .eq(comparator_2_eq));  // open: gt, lt
  Comparator #(.width(4)) comparator_3 (.a(in2), .b(4'b1001), .eq(comparator_3_eq));  // open: gt, lt
  button_on_of button_on_of_1 (.in_1(and_1_out), .out_2(game_on));
  or or_2 (or_2_out, comparator_2_eq, comparator_3_eq);
  panel panel_1 (.in_1(digit_on_5_7_1_out_3), .out_2(panel_1_out_2));
  panel panel_2 (.in_1(digit_on_5_7_1_out_5), .out_2(panel_2_out_2));
  panel panel_3 (.in_1(digit_on_5_7_1_out_2), .out_2(panel_3_out_2));
  panel panel_4 (.in_1(digit_on_5_7_1_out_6), .out_2(panel_4_out_2));
  digit_on_5_7 digit_on_5_7_1 (
    .in_1(in1), .out_2(digit_on_5_7_1_out_2), .out_5(digit_on_5_7_1_out_5), .out_3(digit_on_5_7_1_out_3),
    .out_6(digit_on_5_7_1_out_6), .out_4(digit_on_5_7_1_out_4));
  panel panel_5 (.in_1(digit_on_5_7_1_out_4), .out_2(panel_5_out_2));
  helper_dislpay helper_dislpay_1 (
    .in_1(game_on), .bus_0_125(out_13), .bus_0_126(out_14), .bus_0_127(out_15), .bus_0_128(out_16),
    .bus_0_129(out_17), .bus_0_130(out_18), .bus_0_131(out_19), .bus_0_93(out_20), .bus_0_94(out_21),
    .bus_0_95(out_22), .bus_0_96(out_23), .bus_0_97(out_24), .bus_0_98(out_25), .bus_0_99(out_26),
    .bus_0_100(out_27), .bus_0_101(out_28), .bus_0_102(out_29), .bus_0_103(out_30), .bus_0_104(out_31),
    .bus_0_105(out_32), .bus_0_106(out_33), .bus_0_107(out_34), .bus_0_108(out_35), .bus_0_109(out_36),
    .bus_0_110(out_37), .bus_0_111(out_38), .bus_0_112(out_39), .bus_0_113(out_40), .bus_0_114(out_41),
    .bus_0_115(out_42), .bus_0_116(out_43), .bus_0_117(out_44), .bus_0_118(out_45), .bus_0_119(out_46),
    .bus_0_120(out_47), .bus_0_121(out_48), .bus_0_122(out_49), .bus_0_123(out_50), .bus_0_124(out_51),
    .bus_0_72({32{1'b0}}), .bus_0_73(panel_3_out_2), .bus_0_74(panel_2_out_2), .bus_0_75(panel_1_out_2),
    .bus_0_76(panel_4_out_2), .bus_0_77(panel_5_out_2), .bus_0_78({32{1'b0}}), .bus_0(part_2_1_data),
    .bus_0_2(part_2_1_data_2), .bus_0_3(part_2_1_data_3), .bus_0_4(part_2_1_data_4),
    .bus_0_5(part_2_1_data_5), .bus_0_6(part_2_1_data_6), .bus_0_7(part_2_1_data_7),
    .bus_0_8(part_2_1_data_8), .bus_0_9(part_2_2_data), .bus_0_10(part_2_2_data_2),
    .bus_0_11(part_2_2_data_3), .bus_0_12(part_2_2_data_4), .bus_0_13(part_2_2_data_5),
    .bus_0_14(part_2_2_data_6), .bus_0_15(part_2_2_data_7), .bus_0_16(part_2_2_data_8),
    .bus_0_33(part_2_3_data), .bus_0_34(part_2_3_data_2), .bus_0_35(part_2_3_data_3),
    .bus_0_36(part_2_3_data_4), .bus_0_37(part_2_3_data_5), .bus_0_38(part_2_3_data_6),
    .bus_0_39(part_2_3_data_7), .bus_0_40(part_2_3_data_8), .bus_0_41(part_2_4_data),
    .bus_0_42(part_2_4_data_2), .bus_0_43(part_2_4_data_3), .bus_0_44(part_2_4_data_4),
    .bus_0_45(part_2_4_data_5), .bus_0_46(part_2_4_data_6), .bus_0_47(part_2_4_data_7),
    .bus_0_48(part_2_4_data_8), .bus_0_65({32{1'b0}}), .bus_0_66({32{1'b0}}), .bus_0_67(32'h790000),
    .bus_0_68(32'h490000), .bus_0_69(32'h490000), .bus_0_70(32'h490000), .bus_0_71(32'h4f0000),
    .bus_0_17({32{1'b0}}), .bus_0_18(32'h7f0000), .bus_0_19(32'h490000), .bus_0_20(32'h490000),
    .bus_0_21(32'h490000), .bus_0_22(32'h490000), .bus_0_23({32{1'b0}}), .bus_0_24(32'h3f0000),
    .bus_0_25(32'h480000), .bus_0_26(32'h480000), .bus_0_27(32'h480000), .bus_0_28(32'h3f0000),
    .bus_0_29(32'h3f80), .bus_0_30(32'h7f2080), .bus_0_31(32'h482480), .bus_0_32(32'h482480),
    .bus_0_49(32'h483780), .bus_0_50(32'h370000), .bus_0_51(32'h1f80), .bus_0_52(32'h2400),
    .bus_0_53(32'h2400), .bus_0_54(32'h2400), .bus_0_55(32'h1f80), .bus_0_56({32{1'b0}}),
    .bus_0_57(32'h3f80), .bus_0_58(32'h800), .bus_0_59(32'h400), .bus_0_60(32'h800), .bus_0_61(32'h3f80),
    .bus_0_62({32{1'b0}}), .bus_0_63(32'h3f80), .bus_0_64(32'h2480), .bus_0_132(out_52), .bus_0_133(out_53),
    .bus_0_134(out_54), .bus_0_135(out_55), .bus_0_136(out_56), .bus_0_137(out_57), .bus_0_138(out_58),
    .bus_0_86({32{1'b0}}), .bus_0_87(panel_10_out_2), .bus_0_88(panel_6_out_2), .bus_0_89(panel_9_out_2),
    .bus_0_90(panel_7_out_2), .bus_0_91(panel_8_out_2), .bus_0_92({32{1'b0}}), .bus_0_79(32'h2480),
    .bus_0_80(32'h2480), .bus_0_81(32'h2480), .bus_0_82({32{1'b0}}), .bus_0_83({32{1'b0}}),
    .bus_0_84({32{1'b0}}), .bus_0_85({32{1'b0}}));
  part_2 part_2_1 (
    .BX(X), .BY(Y), .R1(R0), .R2(R1), .ID({5{1'b0}}), .BX_2(part_2_1_bx_2), .BY_2(part_2_1_by_2),
    .R1_2(part_2_1_r1_2), .R2_2(part_2_1_r2_2), .ID_2(part_2_1_id_2), .data(part_2_1_data),
    .data_2(part_2_1_data_2), .data_3(part_2_1_data_3), .data_4(part_2_1_data_4), .data_5(part_2_1_data_5),
    .data_6(part_2_1_data_6), .data_7(part_2_1_data_7), .data_8(part_2_1_data_8));
  part_2 part_2_2 (
    .BX(part_2_1_bx_2), .BY(part_2_1_by_2), .R1(part_2_1_r1_2), .R2(part_2_1_r2_2), .ID(part_2_1_id_2),
    .BX_2(part_2_2_bx_2), .BY_2(part_2_2_by_2), .R1_2(part_2_2_r1_2), .R2_2(part_2_2_r2_2),
    .ID_2(part_2_2_id_2), .data(part_2_2_data), .data_2(part_2_2_data_2), .data_3(part_2_2_data_3),
    .data_4(part_2_2_data_4), .data_5(part_2_2_data_5), .data_6(part_2_2_data_6), .data_7(part_2_2_data_7),
    .data_8(part_2_2_data_8));
  part_2 part_2_3 (
    .BX(part_2_2_bx_2), .BY(part_2_2_by_2), .R1(part_2_2_r1_2), .R2(part_2_2_r2_2), .ID(part_2_2_id_2),
    .BX_2(part_2_3_bx_2), .BY_2(part_2_3_by_2), .R1_2(part_2_3_r1_2), .R2_2(part_2_3_r2_2),
    .ID_2(part_2_3_id_2), .data(part_2_3_data), .data_2(part_2_3_data_2), .data_3(part_2_3_data_3),
    .data_4(part_2_3_data_4), .data_5(part_2_3_data_5), .data_6(part_2_3_data_6), .data_7(part_2_3_data_7),
    .data_8(part_2_3_data_8));
  panel panel_6 (.in_1(digit_on_5_7_2_out_5), .out_2(panel_6_out_2));
  panel panel_7 (.in_1(digit_on_5_7_2_out_6), .out_2(panel_7_out_2));
  panel panel_8 (.in_1(digit_on_5_7_2_out_4), .out_2(panel_8_out_2));
  panel panel_9 (.in_1(digit_on_5_7_2_out_3), .out_2(panel_9_out_2));
  panel panel_10 (.in_1(digit_on_5_7_2_out_2), .out_2(panel_10_out_2));
  part_2 part_2_4 (
    .BX(part_2_3_bx_2), .BY(part_2_3_by_2), .R1(part_2_3_r1_2), .R2(part_2_3_r2_2), .ID(part_2_3_id_2),
    .data(part_2_4_data), .data_2(part_2_4_data_2), .data_3(part_2_4_data_3), .data_4(part_2_4_data_4),
    .data_5(part_2_4_data_5), .data_6(part_2_4_data_6), .data_7(part_2_4_data_7), .data_8(part_2_4_data_8));  // open: BX_2, BY_2, R1_2, R2_2, ID_2
  digit_on_5_7 digit_on_5_7_2 (
    .in_1(in2), .out_2(digit_on_5_7_2_out_2), .out_5(digit_on_5_7_2_out_5), .out_3(digit_on_5_7_2_out_3),
    .out_6(digit_on_5_7_2_out_6), .out_4(digit_on_5_7_2_out_4));

  assign clava_out = clava_in;
  assign out_11 = {8{1'b1}};
endmodule

module _5_to_8_bit (
  input  [4:0] in_1,
  output [7:0] out_2
);

  Pull_Resistor pull_resistor_1 (.node(out_2[5]));
  Pull_Resistor pull_resistor_2 (.node(out_2[6]));
  Pull_Resistor pull_resistor_3 (.node(out_2[7]));

  assign out_2[4:0] = in_1;
endmodule

module Norm_cord (
  input  [7:0] in_1,
  output [7:0] out_2
);

  wire comparator_1_gt, comparator_2_gt;
  wire [7:0] multiplexer_1_out;

  Comparator comparator_1 (.a(8'h1), .b(in_1), .gt(comparator_1_gt));  // open: eq, lt
  Multiplexer #(.width(8)) multiplexer_1 (
    .in0(in_1), .in1(8'h1), .out(multiplexer_1_out), .sel(comparator_1_gt));  // open: en
  Comparator comparator_2 (.a(multiplexer_1_out), .b(8'h1e), .gt(comparator_2_gt));  // open: eq, lt
  Multiplexer #(.width(8)) multiplexer_2 (
    .in0(multiplexer_1_out), .in1(8'h1e), .out(out_2), .sel(comparator_2_gt));  // open: en
endmodule

module mem_TV_tennis (
  input  [7:0] in_1,
  input  game_on,
  input  reboot,
  input  [6:0] clava,
  output [7:0] out_5,
  output [4:0] X,
  output [4:0] Y,
  output [4:0] Y_r1,
  output [4:0] Y_r0,
  output [3:0] score1,
  output [3:0] score2
);

  counter counter_1 (.ball_x(X), .restart(reboot), .r0(score1), .r1(score2));
  clava clava_1 (.data(clava), ._5_data_out(Y_r0));
  intel_core intel_core_1 (.Y_r0(Y_r0), .Y_ball(Y), .X_Ball(X), .Y_r1(Y_r1), .clr(reboot), .game_on_off(game_on));

  assign out_5 = in_1;

  // Notes on the sheet:
  //   y_r0
endmodule

module digit_on_dislpay_3_5 (
  input  [3:0] in_1,
  output [4:0] out_2,
  output [4:0] out_3,
  output [4:0] out_4
);

  Multiplexer #(.select(4), .width(15)) multiplexer_1 (
    .in0(15'h7e3f), .in1(15'h1f), .in2(15'h5ebd), .in3(15'h56bf), .in4(15'h709f), .in5(15'h76b7),
    .in6(15'h7eb7), .in7(15'h421f), .in8(15'h7ebf), .in9(15'h76bf), .out({out_2, out_3, out_4}), .sel(in_1));  // open: in10, in11, in12, in13, in14, in15, en
endmodule

module helper_dislpay (
  input  in_1,
  input  [31:0] bus_0,
  input  [31:0] bus_0_2,
  input  [31:0] bus_0_3,
  input  [31:0] bus_0_4,
  input  [31:0] bus_0_5,
  input  [31:0] bus_0_6,
  input  [31:0] bus_0_7,
  input  [31:0] bus_0_8,
  input  [31:0] bus_0_9,
  input  [31:0] bus_0_10,
  input  [31:0] bus_0_11,
  input  [31:0] bus_0_12,
  input  [31:0] bus_0_13,
  input  [31:0] bus_0_14,
  input  [31:0] bus_0_15,
  input  [31:0] bus_0_16,
  input  [31:0] bus_0_17,
  input  [31:0] bus_0_18,
  input  [31:0] bus_0_19,
  input  [31:0] bus_0_20,
  input  [31:0] bus_0_21,
  input  [31:0] bus_0_22,
  input  [31:0] bus_0_23,
  input  [31:0] bus_0_24,
  input  [31:0] bus_0_25,
  input  [31:0] bus_0_26,
  input  [31:0] bus_0_27,
  input  [31:0] bus_0_28,
  input  [31:0] bus_0_29,
  input  [31:0] bus_0_30,
  input  [31:0] bus_0_31,
  input  [31:0] bus_0_32,
  input  [31:0] bus_0_33,
  input  [31:0] bus_0_34,
  input  [31:0] bus_0_35,
  input  [31:0] bus_0_36,
  input  [31:0] bus_0_37,
  input  [31:0] bus_0_38,
  input  [31:0] bus_0_39,
  input  [31:0] bus_0_40,
  input  [31:0] bus_0_41,
  input  [31:0] bus_0_42,
  input  [31:0] bus_0_43,
  input  [31:0] bus_0_44,
  input  [31:0] bus_0_45,
  input  [31:0] bus_0_46,
  input  [31:0] bus_0_47,
  input  [31:0] bus_0_48,
  input  [31:0] bus_0_49,
  input  [31:0] bus_0_50,
  input  [31:0] bus_0_51,
  input  [31:0] bus_0_52,
  input  [31:0] bus_0_53,
  input  [31:0] bus_0_54,
  input  [31:0] bus_0_55,
  input  [31:0] bus_0_56,
  input  [31:0] bus_0_57,
  input  [31:0] bus_0_58,
  input  [31:0] bus_0_59,
  input  [31:0] bus_0_60,
  input  [31:0] bus_0_61,
  input  [31:0] bus_0_62,
  input  [31:0] bus_0_63,
  input  [31:0] bus_0_64,
  input  [31:0] bus_0_65,
  input  [31:0] bus_0_66,
  input  [31:0] bus_0_67,
  input  [31:0] bus_0_68,
  input  [31:0] bus_0_69,
  input  [31:0] bus_0_70,
  input  [31:0] bus_0_71,
  input  [31:0] bus_0_72,
  input  [31:0] bus_0_73,
  input  [31:0] bus_0_74,
  input  [31:0] bus_0_75,
  input  [31:0] bus_0_76,
  input  [31:0] bus_0_77,
  input  [31:0] bus_0_78,
  input  [31:0] bus_0_79,
  input  [31:0] bus_0_80,
  input  [31:0] bus_0_81,
  input  [31:0] bus_0_82,
  input  [31:0] bus_0_83,
  input  [31:0] bus_0_84,
  input  [31:0] bus_0_85,
  input  [31:0] bus_0_86,
  input  [31:0] bus_0_87,
  input  [31:0] bus_0_88,
  input  [31:0] bus_0_89,
  input  [31:0] bus_0_90,
  input  [31:0] bus_0_91,
  input  [31:0] bus_0_92,
  output [31:0] bus_0_93,
  output [31:0] bus_0_94,
  output [31:0] bus_0_95,
  output [31:0] bus_0_96,
  output [31:0] bus_0_97,
  output [31:0] bus_0_98,
  output [31:0] bus_0_99,
  output [31:0] bus_0_100,
  output [31:0] bus_0_101,
  output [31:0] bus_0_102,
  output [31:0] bus_0_103,
  output [31:0] bus_0_104,
  output [31:0] bus_0_105,
  output [31:0] bus_0_106,
  output [31:0] bus_0_107,
  output [31:0] bus_0_108,
  output [31:0] bus_0_109,
  output [31:0] bus_0_110,
  output [31:0] bus_0_111,
  output [31:0] bus_0_112,
  output [31:0] bus_0_113,
  output [31:0] bus_0_114,
  output [31:0] bus_0_115,
  output [31:0] bus_0_116,
  output [31:0] bus_0_117,
  output [31:0] bus_0_118,
  output [31:0] bus_0_119,
  output [31:0] bus_0_120,
  output [31:0] bus_0_121,
  output [31:0] bus_0_122,
  output [31:0] bus_0_123,
  output [31:0] bus_0_124,
  output [31:0] bus_0_125,
  output [31:0] bus_0_126,
  output [31:0] bus_0_127,
  output [31:0] bus_0_128,
  output [31:0] bus_0_129,
  output [31:0] bus_0_130,
  output [31:0] bus_0_131,
  output [31:0] bus_0_132,
  output [31:0] bus_0_133,
  output [31:0] bus_0_134,
  output [31:0] bus_0_135,
  output [31:0] bus_0_136,
  output [31:0] bus_0_137,
  output [31:0] bus_0_138
);

  wire not_1_out;

  assign bus_0_127 = in_1 ? bus_0_74 : 32'bz;  // Controlled_Buffer controlled_buffer_1
  assign bus_0_126 = in_1 ? bus_0_73 : 32'bz;  // Controlled_Buffer controlled_buffer_2
  assign bus_0_125 = in_1 ? bus_0_72 : 32'bz;  // Controlled_Buffer controlled_buffer_3
  assign bus_0_131 = in_1 ? bus_0_78 : 32'bz;  // Controlled_Buffer controlled_buffer_4
  assign bus_0_130 = in_1 ? bus_0_77 : 32'bz;  // Controlled_Buffer controlled_buffer_5
  assign bus_0_129 = in_1 ? bus_0_76 : 32'bz;  // Controlled_Buffer controlled_buffer_6
  assign bus_0_128 = in_1 ? bus_0_75 : 32'bz;  // Controlled_Buffer controlled_buffer_7
  assign bus_0_95 = in_1 ? bus_0_3 : 32'bz;  // Controlled_Buffer controlled_buffer_8
  assign bus_0_94 = in_1 ? bus_0_2 : 32'bz;  // Controlled_Buffer controlled_buffer_9
  assign bus_0_93 = in_1 ? bus_0 : 32'bz;  // Controlled_Buffer controlled_buffer_10
  assign bus_0_99 = in_1 ? bus_0_7 : 32'bz;  // Controlled_Buffer controlled_buffer_11
  assign bus_0_98 = in_1 ? bus_0_6 : 32'bz;  // Controlled_Buffer controlled_buffer_12
  assign bus_0_97 = in_1 ? bus_0_5 : 32'bz;  // Controlled_Buffer controlled_buffer_13
  assign bus_0_96 = in_1 ? bus_0_4 : 32'bz;  // Controlled_Buffer controlled_buffer_14
  assign bus_0_103 = in_1 ? bus_0_11 : 32'bz;  // Controlled_Buffer controlled_buffer_15
  assign bus_0_102 = in_1 ? bus_0_10 : 32'bz;  // Controlled_Buffer controlled_buffer_16
  assign bus_0_101 = in_1 ? bus_0_9 : 32'bz;  // Controlled_Buffer controlled_buffer_17
  assign bus_0_100 = in_1 ? bus_0_8 : 32'bz;  // Controlled_Buffer controlled_buffer_18
  assign bus_0_107 = in_1 ? bus_0_15 : 32'bz;  // Controlled_Buffer controlled_buffer_19
  assign bus_0_106 = in_1 ? bus_0_14 : 32'bz;  // Controlled_Buffer controlled_buffer_20
  assign bus_0_105 = in_1 ? bus_0_13 : 32'bz;  // Controlled_Buffer controlled_buffer_21
  assign bus_0_104 = in_1 ? bus_0_12 : 32'bz;  // Controlled_Buffer controlled_buffer_22
  assign bus_0_108 = in_1 ? bus_0_16 : 32'bz;  // Controlled_Buffer controlled_buffer_23
  assign bus_0_111 = in_1 ? bus_0_35 : 32'bz;  // Controlled_Buffer controlled_buffer_24
  assign bus_0_110 = in_1 ? bus_0_34 : 32'bz;  // Controlled_Buffer controlled_buffer_25
  assign bus_0_109 = in_1 ? bus_0_33 : 32'bz;  // Controlled_Buffer controlled_buffer_26
  assign bus_0_115 = in_1 ? bus_0_39 : 32'bz;  // Controlled_Buffer controlled_buffer_27
  assign bus_0_114 = in_1 ? bus_0_38 : 32'bz;  // Controlled_Buffer controlled_buffer_28
  assign bus_0_113 = in_1 ? bus_0_37 : 32'bz;  // Controlled_Buffer controlled_buffer_29
  assign bus_0_112 = in_1 ? bus_0_36 : 32'bz;  // Controlled_Buffer controlled_buffer_30
  assign bus_0_119 = in_1 ? bus_0_43 : 32'bz;  // Controlled_Buffer controlled_buffer_31
  assign bus_0_118 = in_1 ? bus_0_42 : 32'bz;  // Controlled_Buffer controlled_buffer_32
  assign bus_0_117 = in_1 ? bus_0_41 : 32'bz;  // Controlled_Buffer controlled_buffer_33
  assign bus_0_116 = in_1 ? bus_0_40 : 32'bz;  // Controlled_Buffer controlled_buffer_34
  assign bus_0_123 = in_1 ? bus_0_47 : 32'bz;  // Controlled_Buffer controlled_buffer_35
  assign bus_0_122 = in_1 ? bus_0_46 : 32'bz;  // Controlled_Buffer controlled_buffer_36
  assign bus_0_121 = in_1 ? bus_0_45 : 32'bz;  // Controlled_Buffer controlled_buffer_37
  assign bus_0_120 = in_1 ? bus_0_44 : 32'bz;  // Controlled_Buffer controlled_buffer_38
  assign bus_0_124 = in_1 ? bus_0_48 : 32'bz;  // Controlled_Buffer controlled_buffer_39
  assign bus_0_133 = in_1 ? bus_0_87 : 32'bz;  // Controlled_Buffer controlled_buffer_40
  assign bus_0_132 = in_1 ? bus_0_86 : 32'bz;  // Controlled_Buffer controlled_buffer_41
  assign bus_0_137 = in_1 ? bus_0_91 : 32'bz;  // Controlled_Buffer controlled_buffer_42
  assign bus_0_136 = in_1 ? bus_0_90 : 32'bz;  // Controlled_Buffer controlled_buffer_43
  assign bus_0_135 = in_1 ? bus_0_89 : 32'bz;  // Controlled_Buffer controlled_buffer_44
  assign bus_0_134 = in_1 ? bus_0_88 : 32'bz;  // Controlled_Buffer controlled_buffer_45
  assign bus_0_138 = in_1 ? bus_0_92 : 32'bz;  // Controlled_Buffer controlled_buffer_46
  assign bus_0_125 = not_1_out ? bus_0_65 : 32'bz;  // Controlled_Buffer controlled_buffer_47
  assign bus_0_129 = not_1_out ? bus_0_69 : 32'bz;  // Controlled_Buffer controlled_buffer_48
  assign bus_0_128 = not_1_out ? bus_0_68 : 32'bz;  // Controlled_Buffer controlled_buffer_49
  assign bus_0_127 = not_1_out ? bus_0_67 : 32'bz;  // Controlled_Buffer controlled_buffer_50
  assign bus_0_126 = not_1_out ? bus_0_66 : 32'bz;  // Controlled_Buffer controlled_buffer_51
  assign bus_0_131 = not_1_out ? bus_0_71 : 32'bz;  // Controlled_Buffer controlled_buffer_52
  assign bus_0_130 = not_1_out ? bus_0_70 : 32'bz;  // Controlled_Buffer controlled_buffer_53
  assign bus_0_94 = not_1_out ? bus_0_18 : 32'bz;  // Controlled_Buffer controlled_buffer_54
  assign bus_0_93 = not_1_out ? bus_0_17 : 32'bz;  // Controlled_Buffer controlled_buffer_55
  assign bus_0_98 = not_1_out ? bus_0_22 : 32'bz;  // Controlled_Buffer controlled_buffer_56
  assign bus_0_97 = not_1_out ? bus_0_21 : 32'bz;  // Controlled_Buffer controlled_buffer_57
  assign bus_0_96 = not_1_out ? bus_0_20 : 32'bz;  // Controlled_Buffer controlled_buffer_58
  assign bus_0_95 = not_1_out ? bus_0_19 : 32'bz;  // Controlled_Buffer controlled_buffer_59
  assign bus_0_102 = not_1_out ? bus_0_26 : 32'bz;  // Controlled_Buffer controlled_buffer_60
  assign bus_0_101 = not_1_out ? bus_0_25 : 32'bz;  // Controlled_Buffer controlled_buffer_61
  assign bus_0_100 = not_1_out ? bus_0_24 : 32'bz;  // Controlled_Buffer controlled_buffer_62
  assign bus_0_99 = not_1_out ? bus_0_23 : 32'bz;  // Controlled_Buffer controlled_buffer_63
  assign bus_0_106 = not_1_out ? bus_0_30 : 32'bz;  // Controlled_Buffer controlled_buffer_64
  assign bus_0_105 = not_1_out ? bus_0_29 : 32'bz;  // Controlled_Buffer controlled_buffer_65
  assign bus_0_104 = not_1_out ? bus_0_28 : 32'bz;  // Controlled_Buffer controlled_buffer_66
  assign bus_0_103 = not_1_out ? bus_0_27 : 32'bz;  // Controlled_Buffer controlled_buffer_67
  assign bus_0_108 = not_1_out ? bus_0_32 : 32'bz;  // Controlled_Buffer controlled_buffer_68
  assign bus_0_107 = not_1_out ? bus_0_31 : 32'bz;  // Controlled_Buffer controlled_buffer_69
  assign bus_0_110 = not_1_out ? bus_0_50 : 32'bz;  // Controlled_Buffer controlled_buffer_70
  assign bus_0_109 = not_1_out ? bus_0_49 : 32'bz;  // Controlled_Buffer controlled_buffer_71
  assign bus_0_114 = not_1_out ? bus_0_54 : 32'bz;  // Controlled_Buffer controlled_buffer_72
  assign bus_0_113 = not_1_out ? bus_0_53 : 32'bz;  // Controlled_Buffer controlled_buffer_73
  assign bus_0_112 = not_1_out ? bus_0_52 : 32'bz;  // Controlled_Buffer controlled_buffer_74
  assign bus_0_111 = not_1_out ? bus_0_51 : 32'bz;  // Controlled_Buffer controlled_buffer_75
  assign bus_0_118 = not_1_out ? bus_0_58 : 32'bz;  // Controlled_Buffer controlled_buffer_76
  assign bus_0_117 = not_1_out ? bus_0_57 : 32'bz;  // Controlled_Buffer controlled_buffer_77
  assign bus_0_116 = not_1_out ? bus_0_56 : 32'bz;  // Controlled_Buffer controlled_buffer_78
  assign bus_0_115 = not_1_out ? bus_0_55 : 32'bz;  // Controlled_Buffer controlled_buffer_79
  assign bus_0_122 = not_1_out ? bus_0_62 : 32'bz;  // Controlled_Buffer controlled_buffer_80
  assign bus_0_121 = not_1_out ? bus_0_61 : 32'bz;  // Controlled_Buffer controlled_buffer_81
  assign bus_0_120 = not_1_out ? bus_0_60 : 32'bz;  // Controlled_Buffer controlled_buffer_82
  assign bus_0_119 = not_1_out ? bus_0_59 : 32'bz;  // Controlled_Buffer controlled_buffer_83
  not not_1 (not_1_out, in_1);
  assign bus_0_124 = not_1_out ? bus_0_64 : 32'bz;  // Controlled_Buffer controlled_buffer_84
  assign bus_0_123 = not_1_out ? bus_0_63 : 32'bz;  // Controlled_Buffer controlled_buffer_85
  assign bus_0_132 = not_1_out ? bus_0_79 : 32'bz;  // Controlled_Buffer controlled_buffer_86
  assign bus_0_136 = not_1_out ? bus_0_83 : 32'bz;  // Controlled_Buffer controlled_buffer_87
  assign bus_0_135 = not_1_out ? bus_0_82 : 32'bz;  // Controlled_Buffer controlled_buffer_88
  assign bus_0_134 = not_1_out ? bus_0_81 : 32'bz;  // Controlled_Buffer controlled_buffer_89
  assign bus_0_133 = not_1_out ? bus_0_80 : 32'bz;  // Controlled_Buffer controlled_buffer_90
  assign bus_0_138 = not_1_out ? bus_0_85 : 32'bz;  // Controlled_Buffer controlled_buffer_91
  assign bus_0_137 = not_1_out ? bus_0_84 : 32'bz;  // Controlled_Buffer controlled_buffer_92

  // Other names for the same wires on the sheet: vec_adr = in_1
endmodule

module fragment_logic (
  input  in_1,
  input  in_2,
  output out_3
);

  Register #(.width(1)) register_1 (.D(in_1), .en(in_1), .Q(out_3), .clk(in_1), .clr(in_2));
endmodule

module digit_on_5_7 (
  input  [3:0] in_1,
  output [6:0] out_2,
  output [6:0] out_3,
  output [6:0] out_4,
  output [6:0] out_5,
  output [6:0] out_6
);

  wire [6:0] undriven, undriven_2, undriven_3, undriven_4, undriven_5, undriven_6, undriven_7, undriven_8,
       undriven_9, undriven_10, undriven_11, undriven_12, undriven_13, undriven_14, undriven_15, undriven_16,
       undriven_17, undriven_18, undriven_19, undriven_20, undriven_21, undriven_22, undriven_23,
       undriven_24, undriven_25, undriven_26, undriven_27, undriven_28, undriven_29, undriven_30;

  Multiplexer #(.select(4), .width(7)) multiplexer_1 (
    .in0({7{1'b1}}), .in1({7{1'b0}}), .in2(7'b1001111), .in3(7'b1001001), .in4(7'b1111000), .in5(7'b1111001),
    .in6({7{1'b1}}), .in7(7'b1000000), .in8({7{1'b1}}), .in9(7'b1111001), .in10(undriven_25),
    .in11(undriven_26), .in12(undriven_27), .in13(undriven_28), .in14(undriven_29), .in15(undriven_30),
    .out(out_2), .sel(in_1));  // open: en
  Multiplexer #(.select(4), .width(7)) multiplexer_2 (
    .in0(7'b1000001), .in1({7{1'b0}}), .in2(7'b1001001), .in3(7'b1001001), .in4(7'b0001000),
    .in5(7'b1001001), .in6(7'b1001001), .in7(7'b1000000), .in8(7'b1001001), .in9(7'b1001001),
    .in10(undriven), .in11(undriven_13), .in12(undriven_2), .in13(undriven_14), .in14(undriven_3),
    .in15(undriven_15), .out(out_5), .sel(in_1));  // open: en
  Multiplexer #(.select(4), .width(7)) multiplexer_3 (
    .in0(7'b1000001), .in1({7{1'b0}}), .in2(7'b1001001), .in3(7'b1001001), .in4(7'b0001000),
    .in5(7'b1001001), .in6(7'b1001001), .in7(7'b1000000), .in8(7'b1001001), .in9(7'b1001001),
    .in10(undriven_4), .in11(undriven_16), .in12(undriven_5), .in13(undriven_17), .in14(undriven_6),
    .in15(undriven_18), .out(out_3), .sel(in_1));  // open: en
  Multiplexer #(.select(4), .width(7)) multiplexer_4 (
    .in0(7'b1000001), .in1({7{1'b0}}), .in2(7'b1001001), .in3(7'b1001001), .in4(7'b0001000),
    .in5(7'b1001001), .in6(7'b1001001), .in7(7'b1000000), .in8(7'b1001001), .in9(7'b1001001),
    .in10(undriven_7), .in11(undriven_19), .in12(undriven_8), .in13(undriven_20), .in14(undriven_9),
    .in15(undriven_21), .out(out_6), .sel(in_1));  // open: en
  Multiplexer #(.select(4), .width(7)) multiplexer_5 (
    .in0({7{1'b1}}), .in1({7{1'b1}}), .in2(7'b1111001), .in3({7{1'b1}}), .in4({7{1'b1}}), .in5(7'b1001111),
    .in6(7'b1001111), .in7({7{1'b1}}), .in8({7{1'b1}}), .in9({7{1'b1}}), .in10(undriven_10),
    .in11(undriven_22), .in12(undriven_11), .in13(undriven_23), .in14(undriven_12), .in15(undriven_24),
    .out(out_4), .sel(in_1));  // open: en
endmodule

module button_on_of (
  input  in_1,
  output out_2
);

  wire and_1_out, and_2_out, fragment_logic_2_out_3;

  fragment_logic fragment_logic_1 (.in_1(in_1), .in_2(and_2_out), .out_3(out_2));
  and and_1 (and_1_out, ~in_1, out_2);  // AND_Gate
  fragment_logic fragment_logic_2 (.in_1(and_1_out), .in_2(and_2_out), .out_3(fragment_logic_2_out_3));
  and and_2 (and_2_out, fragment_logic_2_out_3, in_1);
endmodule

module panel (
  input  [6:0] in_1,
  output [31:0] out_2
);

  Pull_Resistor pull_resistor_1 (.node(out_2[31]));

  assign out_2[30:0] = {{7{out_2[31]}}, in_1, {17{out_2[31]}}};
endmodule

module alpha0 (
  input  [7:0] \new ,
  input  [7:0] old,
  input  [7:0] v_0,
  input  sign,
  output [7:0] y_max,
  output [7:0] x_max,
  output sign_2
);

  wire clock_1_out, clock_2_out, clock_3_out, clock_4_out, clock_5_out, comparator_1_gt, comparator_2_lt,
       comparator_3_lt, comparator_4_lt, not_1_out, not_2_out;
  wire [7:0] adder_1_out, adder_2_out, demultiplexer_1_out0, demultiplexer_1_out1, divider_1_out,
       divider_2_out, multiplexer_1_out, multiplexer_2_out, multiplexer_3_out, multiplexer_4_out, neg_1_out,
       register_1_q, register_2_q, register_4_q, register_5_q, subtractor_1_out, \модуль_1_out_2 ,
       \модуль_2_out_2 , \модуль_3_out_2 ;

  Subtractor subtractor_1 (.a(\new ), .b(old), .out(subtractor_1_out));  // open: bin, bout
  Clock clock_1 (.out(clock_1_out));
  not not_1 (not_1_out, sign);
  Register register_1 (.D(subtractor_1_out), .en(sign), .Q(register_1_q), .clk(clock_1_out));  // open: clr
  Register register_2 (.D(v_0), .en(not_1_out), .Q(register_2_q), .clk(clock_2_out));  // open: clr
  Clock clock_2 (.out(clock_2_out));
  \модуль  \u_модуль_1  (.in_1(register_1_q), .out_2(\модуль_1_out_2 ));
  Divider divider_1 (.a(\модуль_1_out_2 ), .b(8'h4), .out(divider_1_out));  // open: upper, rem
  Divider divider_2 (.a(register_2_q), .b(8'h2), .out(divider_2_out));  // open: upper, rem
  neg neg_1 (.in(divider_1_out), .out(neg_1_out));
  \модуль  \u_модуль_2  (.in_1(adder_1_out), .out_2(\модуль_2_out_2 ));
  Adder adder_1 (.a(register_2_q), .b(register_1_q), .out(adder_1_out));  // open: cin, cout
  Multiplexer #(.width(8)) multiplexer_1 (
    .in0(divider_1_out), .in1(neg_1_out), .out(multiplexer_1_out), .sel(register_1_q[7]));  // open: en
  Adder adder_2 (.a(multiplexer_1_out), .b(divider_2_out), .out(adder_2_out));  // open: cin, cout
  \модуль  \u_модуль_3  (.in_1(adder_2_out), .out_2(\модуль_3_out_2 ));
  Comparator comparator_1 (.a(\модуль_2_out_2 ), .b(8'h4), .gt(comparator_1_gt));  // open: eq, lt
  Demultiplexer #(.width(8)) demultiplexer_1 (
    .out0(demultiplexer_1_out0), .out1(demultiplexer_1_out1), .in(multiplexer_2_out), .sel(comparator_2_lt));  // open: en
  Multiplexer #(.width(8)) multiplexer_2 (
    .in0(\модуль_2_out_2 ), .in1(8'h4), .out(multiplexer_2_out), .sel(comparator_1_gt));  // open: en
  Comparator comparator_2 (.a(\модуль_3_out_2 ), .b(8'h1), .lt(comparator_2_lt));  // open: gt, eq
  not not_2 (not_2_out, comparator_2_lt);
  Clock clock_3 (.out(clock_3_out));
  Comparator comparator_3 (.a(demultiplexer_1_out0), .b(8'h2), .lt(comparator_3_lt));  // open: gt, eq
  Comparator comparator_4 (.a(demultiplexer_1_out1), .b(8'h2), .lt(comparator_4_lt));  // open: gt, eq
  Register #(.width(1)) register_3 (.D(not_2_out), .en(sign), .Q(sign_2), .clk(clock_3_out));  // open: clr
  Multiplexer #(.width(8)) multiplexer_3 (
    .in0(demultiplexer_1_out0), .in1(8'h2), .out(multiplexer_3_out), .sel(comparator_3_lt));  // open: en
  Clock clock_4 (.out(clock_4_out));
  Multiplexer #(.width(8)) multiplexer_4 (
    .in0(demultiplexer_1_out1), .in1(8'h2), .out(multiplexer_4_out), .sel(comparator_4_lt));  // open: en
  Register register_4 (.D(multiplexer_4_out), .en(sign), .Q(register_4_q), .clk(clock_5_out));  // open: clr
  Clock clock_5 (.out(clock_5_out));
  assign y_max = sign ? register_5_q : 8'bz;  // Controlled_Buffer controlled_buffer_1
  Register register_5 (.D(multiplexer_3_out), .en(sign), .Q(register_5_q), .clk(clock_4_out));  // open: clr
  assign x_max = sign ? register_4_q : 8'bz;  // Controlled_Buffer controlled_buffer_2
endmodule
