// Logisim project tic_tac_proj.circ as structural Verilog
module main (
  input  on_off
);

  wire _1, _2, _3, _4, _5, _6, _7, _8, _9, reboot, video_2_1_out_12, video_2_1_out_28,
       \video_2_1_крестик_win ;
  wire [4:0] video_2_1_out_13, video_2_1_out_14, video_2_1_out_15, video_2_1_out_16, video_2_1_out_17,
       video_2_1_out_18, video_2_1_out_19, video_2_1_out_20, video_2_1_out_21, video_2_1_out_22,
       video_2_1_out_23, video_2_1_out_24, video_2_1_out_25, video_2_1_out_26, video_2_1_out_27,
       video_2_1_out_29, video_2_1_out_30, video_2_1_out_31, video_2_1_out_32, video_2_1_out_33,
       video_2_1_out_34, video_2_1_out_35, video_2_1_out_36, video_2_1_out_37, video_2_1_out_38,
       video_2_1_out_39, video_2_1_out_40, video_2_1_out_41, video_2_1_out_42, video_2_1_out_43,
       video_2_1_out_44, video_2_1_out_45, video_2_1_out_46, video_2_1_out_47, video_2_1_out_48,
       video_2_1_out_49, video_2_1_out_50, video_2_1_out_51, video_2_1_out_52, video_2_1_out_53,
       video_2_1_out_54, video_2_1_out_55, video_2_1_out_56, video_2_1_out_57, video_2_1_out_58;

  DotMatrix #(.matrixrows(5)) dotmatrix_1 (
    .col0(video_2_1_out_18), .col1(video_2_1_out_19), .col2(video_2_1_out_20), .col3(video_2_1_out_21),
    .col4(video_2_1_out_22));
  DotMatrix #(.matrixrows(5)) dotmatrix_2 (
    .col0(video_2_1_out_13), .col1(video_2_1_out_14), .col2(video_2_1_out_15), .col3(video_2_1_out_16),
    .col4(video_2_1_out_17));
  DotMatrix #(.matrixrows(5)) dotmatrix_3 (
    .col0(video_2_1_out_29), .col1(video_2_1_out_30), .col2(video_2_1_out_31), .col3(video_2_1_out_32),
    .col4(video_2_1_out_33));
  DotMatrix #(.matrixrows(5)) dotmatrix_4 (
    .col0(video_2_1_out_34), .col1(video_2_1_out_35), .col2(video_2_1_out_36), .col3(video_2_1_out_37),
    .col4(video_2_1_out_38));
  DotMatrix #(.matrixrows(5)) dotmatrix_5 (
    .col0(video_2_1_out_44), .col1(video_2_1_out_45), .col2(video_2_1_out_46), .col3(video_2_1_out_47),
    .col4(video_2_1_out_48));
  DotMatrix #(.matrixrows(5)) dotmatrix_6 (
    .col0(video_2_1_out_49), .col1(video_2_1_out_50), .col2(video_2_1_out_51), .col3(video_2_1_out_52),
    .col4(video_2_1_out_53));
  Button button_1 (.out(_1));
  Button button_2 (.out(_4));
  Button button_3 (.out(_7));
  DotMatrix #(.matrixrows(5)) dotmatrix_7 (
    .col0(video_2_1_out_23), .col1(video_2_1_out_24), .col2(video_2_1_out_25), .col3(video_2_1_out_26),
    .col4(video_2_1_out_27));
  DotMatrix #(.matrixrows(5)) dotmatrix_8 (
    .col0(video_2_1_out_39), .col1(video_2_1_out_40), .col2(video_2_1_out_41), .col3(video_2_1_out_42),
    .col4(video_2_1_out_43));
  DotMatrix #(.matrixrows(5)) dotmatrix_9 (
    .col0(video_2_1_out_54), .col1(video_2_1_out_55), .col2(video_2_1_out_56), .col3(video_2_1_out_57),
    .col4(video_2_1_out_58));
  Button button_4 (.out(_2));
  Button button_5 (.out(_3));
  Button button_6 (.out(_6));
  Button button_7 (.out(_5));
  Button button_8 (.out(_9));
  Button button_9 (.out(_8));
  Button button_10 (.out(reboot));
  dls1 dls1_1 ();
  video_2 video_2_1 (
    .\кнопка_1 (_1), .\кнопка_2 (_2), .\кнопка_3 (_3), .\кнопка_4 (_4), .reboot(reboot),
    .out_13(video_2_1_out_13), .out_29(video_2_1_out_29), .out_44(video_2_1_out_44),
    .out_14(video_2_1_out_14), .out_30(video_2_1_out_30), .out_45(video_2_1_out_45),
    .out_15(video_2_1_out_15), .out_31(video_2_1_out_31), .out_46(video_2_1_out_46),
    .out_16(video_2_1_out_16), .out_32(video_2_1_out_32), .out_47(video_2_1_out_47),
    .out_17(video_2_1_out_17), .out_33(video_2_1_out_33), .out_48(video_2_1_out_48),
    .out_18(video_2_1_out_18), .out_34(video_2_1_out_34), .out_49(video_2_1_out_49),
    .out_19(video_2_1_out_19), .out_35(video_2_1_out_35), .out_50(video_2_1_out_50),
    .out_20(video_2_1_out_20), .out_36(video_2_1_out_36), .out_51(video_2_1_out_51),
    .out_21(video_2_1_out_21), .out_37(video_2_1_out_37), .out_52(video_2_1_out_52),
    .out_22(video_2_1_out_22), .out_38(video_2_1_out_38), .out_53(video_2_1_out_53),
    .out_23(video_2_1_out_23), .out_39(video_2_1_out_39), .out_54(video_2_1_out_54),
    .out_24(video_2_1_out_24), .out_40(video_2_1_out_40), .out_55(video_2_1_out_55),
    .out_25(video_2_1_out_25), .out_41(video_2_1_out_41), .out_56(video_2_1_out_56),
    .out_26(video_2_1_out_26), .out_42(video_2_1_out_42), .out_57(video_2_1_out_57),
    .out_27(video_2_1_out_27), .out_43(video_2_1_out_43), .out_58(video_2_1_out_58), .\кнопка_9 (_9),
    .\кнопка_8 (_8), .\кнопка_7 (_7), .\кнопка_6 (_6), .\кнопка_5 (_5),
    .\крестик_win (\video_2_1_крестик_win ), .out_28(video_2_1_out_28), .out_12(video_2_1_out_12),
    .in_11(on_off));
  dis dis_1 ();

  // Notes on the sheet:
  //   победа ноликов
  //   победа крестиков
  //   ничья
endmodule

module video (
  input  \крестик ,
  input  \нолик ,
  input  reboot,
  output [4:0] out_4,
  output [4:0] out_5,
  output [4:0] out_6,
  output [4:0] out_7,
  output [4:0] out_8,
  output \нолик_2 ,
  output \крестик_2 ,
  output \кнопка_горит 
);

  wire and_1_out, clock_1_out, comparator_1_eq, comparator_2_eq, comparator_3_eq, or_1_out;
  wire [1:0] priority_encoder_1_out;
  wire [24:0] multiplexer_1_out;

  Multiplexer #(.select(2), .width(25), .disabled(0), .enable("false")) multiplexer_1 (
    .in0({25{1'b0}}), .in1(25'h1151151), .in2(25'h1f8c63f), .out(multiplexer_1_out),
    .sel(priority_encoder_1_out));  // open: in3
  or or_1 (or_1_out, \крестик , \нолик );
  Priority_Encoder #(.select(2)) priority_encoder_1 (
    .in0(1'b1), .in1(\крестик ), .in2(\нолик ), .out(priority_encoder_1_out));  // open: in3, gs, en_out, en_in
  and and_1 (and_1_out, or_1_out, comparator_1_eq);
  Register #(.width(25)) register_1 (
    .D(multiplexer_1_out), .en(and_1_out), .Q({out_4, out_5, out_6, out_7, out_8}), .clk(clock_1_out),
    .clr(reboot));
  Clock clock_1 (.out(clock_1_out));
  Comparator #(.width(25)) comparator_1 (
    .a({out_4, out_5, out_6, out_7, out_8}), .b({25{1'b0}}), .eq(comparator_1_eq));  // open: gt, lt
  not not_1 (\кнопка_горит , comparator_1_eq);
  Comparator #(.width(25), .mode("unsigned")) comparator_2 (
    .a({out_4, out_5, out_6, out_7, out_8}), .b(25'h1f8c63f), .eq(comparator_2_eq));  // open: gt, lt
  Comparator #(.width(25), .mode("unsigned")) comparator_3 (
    .a({out_4, out_5, out_6, out_7, out_8}), .b(25'h1151151), .eq(comparator_3_eq));  // open: gt, lt
  assign \нолик_2  = comparator_2_eq ? \кнопка_горит  : 1'bz;  // Controlled_Buffer controlled_buffer_1
  Pull_Resistor pull_resistor_1 (.node(\нолик_2 ));
  assign \крестик_2  = \кнопка_горит  ? comparator_3_eq : 1'bz;  // Controlled_Buffer controlled_buffer_2
  Pull_Resistor pull_resistor_2 (.node(\крестик_2 ));

  // Notes on the sheet:
  //   крестик
  //   нолик
endmodule

module video_2 (
  input  \кнопка_1 ,
  input  \кнопка_2 ,
  input  \кнопка_3 ,
  input  \кнопка_4 ,
  input  \кнопка_5 ,
  input  reboot,
  input  \кнопка_6 ,
  input  \кнопка_7 ,
  input  \кнопка_8 ,
  input  \кнопка_9 ,
  input  in_11,
  output out_12,
  output [4:0] out_13,
  output [4:0] out_14,
  output [4:0] out_15,
  output [4:0] out_16,
  output [4:0] out_17,
  output [4:0] out_18,
  output [4:0] out_19,
  output [4:0] out_20,
  output [4:0] out_21,
  output [4:0] out_22,
  output [4:0] out_23,
  output [4:0] out_24,
  output [4:0] out_25,
  output [4:0] out_26,
  output [4:0] out_27,
  output out_28,
  output [4:0] out_29,
  output [4:0] out_30,
  output [4:0] out_31,
  output [4:0] out_32,
  output [4:0] out_33,
  output [4:0] out_34,
  output [4:0] out_35,
  output [4:0] out_36,
  output [4:0] out_37,
  output [4:0] out_38,
  output [4:0] out_39,
  output [4:0] out_40,
  output [4:0] out_41,
  output [4:0] out_42,
  output [4:0] out_43,
  output [4:0] out_44,
  output [4:0] out_45,
  output [4:0] out_46,
  output [4:0] out_47,
  output [4:0] out_48,
  output [4:0] out_49,
  output [4:0] out_50,
  output [4:0] out_51,
  output [4:0] out_52,
  output [4:0] out_53,
  output [4:0] out_54,
  output [4:0] out_55,
  output [4:0] out_56,
  output [4:0] out_57,
  output [4:0] out_58,
  output \крестик_win 
);

  wire _1, _2, _3, _4, _5, _6, _7, _8, _9, and_1_out, and_2_out, and_3_out, and_4_out, and_5_out, and_6_out,
       and_7_out, and_8_out, and_9_out, and_11_out, and_12_out, and_13_out, and_14_out, and_15_out,
       and_16_out, and_17_out, and_18_out, clock_1_out, clock_2_out, comparator_1_eq,
       controlled_buffer_1_out, controlled_buffer_2_out, controlled_buffer_3_out, controlled_buffer_4_out,
       controlled_buffer_5_out, controlled_buffer_6_out, controlled_buffer_7_out, controlled_buffer_8_out,
       demultiplexer_1_out0, demultiplexer_1_out1, demultiplexer_1_out2, demultiplexer_1_out3,
       demultiplexer_1_out4, demultiplexer_1_out5, demultiplexer_1_out6, demultiplexer_1_out7,
       demultiplexer_1_out8, demultiplexer_2_out0, demultiplexer_2_out1, demultiplexer_3_out0,
       demultiplexer_3_out1, demultiplexer_4_out0, demultiplexer_4_out1, demultiplexer_5_out0,
       demultiplexer_5_out1, demultiplexer_6_out0, demultiplexer_6_out1, demultiplexer_7_out0,
       demultiplexer_7_out1, demultiplexer_8_out0, demultiplexer_8_out1, demultiplexer_9_out0,
       demultiplexer_9_out1, demultiplexer_10_out0, demultiplexer_10_out1, n0, n1, n2, n3, n4, n5, n6, n7,
       n8, not_1_out, not_2_out, odd_parity_1_out, or_11_out, or_13_out, priority_encoder_1_gs,
       proc_1_process, pull_resistor_9_node, pull_resistor_10_node, register_1_q, up, v0, v1, v2, v3, v4, v5,
       v6, v7, v8, \video_1_кнопка_горит , \video_2_кнопка_горит , \video_3_кнопка_горит ,
       \video_4_кнопка_горит , \video_5_кнопка_горит , \video_6_кнопка_горит , \video_7_кнопка_горит ,
       \video_8_кнопка_горит , \video_9_кнопка_горит ;
  wire [3:0] bit_extender_1_out, priority_encoder_1_out;
  wire [7:0] bit_extender_2_out, counter_1_q, update;

  assign controlled_buffer_1_out = pull_resistor_10_node ? \кнопка_1  : 1'bz;  // Controlled_Buffer controlled_buffer_1
  assign controlled_buffer_2_out = pull_resistor_10_node ? \кнопка_2  : 1'bz;  // Controlled_Buffer controlled_buffer_2
  assign controlled_buffer_3_out = pull_resistor_10_node ? \кнопка_3  : 1'bz;  // Controlled_Buffer controlled_buffer_3
  assign controlled_buffer_4_out = pull_resistor_10_node ? \кнопка_4  : 1'bz;  // Controlled_Buffer controlled_buffer_4
  Register #(.width(1)) register_1 (
    .D(or_11_out), .en(or_11_out), .Q(register_1_q), .clk(or_11_out), .clr(comparator_1_eq));
  Clock clock_1 (.out(clock_1_out));
  Pull_Resistor pull_resistor_1 (.node(controlled_buffer_1_out));
  Pull_Resistor pull_resistor_2 (.node(controlled_buffer_2_out));
  Pull_Resistor pull_resistor_3 (.node(controlled_buffer_3_out));
  Pull_Resistor pull_resistor_4 (.node(controlled_buffer_4_out));
  assign controlled_buffer_5_out = pull_resistor_10_node ? \кнопка_5  : 1'bz;  // Controlled_Buffer controlled_buffer_5
  Pull_Resistor pull_resistor_5 (.node(controlled_buffer_5_out));
  assign controlled_buffer_6_out = pull_resistor_10_node ? \кнопка_6  : 1'bz;  // Controlled_Buffer controlled_buffer_6
  Pull_Resistor pull_resistor_6 (.node(controlled_buffer_6_out));
  assign controlled_buffer_7_out = pull_resistor_10_node ? \кнопка_7  : 1'bz;  // Controlled_Buffer controlled_buffer_7
  assign controlled_buffer_8_out = pull_resistor_10_node ? \кнопка_8  : 1'bz;  // Controlled_Buffer controlled_buffer_8
  not not_1 (not_1_out, or_11_out);
  Clock clock_2 (.out(clock_2_out));
  and and_1 (and_1_out, register_1_q, clock_1_out);
  Pull_Resistor pull_resistor_7 (.node(controlled_buffer_7_out));
  Pull_Resistor pull_resistor_8 (.node(controlled_buffer_8_out));
  Pull_Resistor pull_resistor_9 (.node(pull_resistor_9_node));
  assign pull_resistor_9_node = pull_resistor_10_node ? \кнопка_9  : 1'bz;  // Controlled_Buffer controlled_buffer_9
  Pull_Resistor pull_resistor_10 (.node(pull_resistor_10_node));
  Register #(.width(1)) register_2 (
    .D(not_1_out), .en(not_1_out), .Q(pull_resistor_10_node), .clk(clock_2_out), .clr(comparator_1_eq));
  Counter counter_1 (.Q(counter_1_q), .clk(and_1_out), .clr(comparator_1_eq));  // open: load, D, count, carry
  Demultiplexer #(.select(4), .disabled(0)) demultiplexer_1 (
    .out0(demultiplexer_1_out0), .out1(demultiplexer_1_out1), .out2(demultiplexer_1_out2),
    .out3(demultiplexer_1_out3), .out4(demultiplexer_1_out4), .out5(demultiplexer_1_out5),
    .out6(demultiplexer_1_out6), .out7(demultiplexer_1_out7), .out8(demultiplexer_1_out8), .in(1'b1),
    .sel(bit_extender_1_out), .en(up));  // open: out9, out10, out11, out12, out13, out14, out15
  Bit_Extender #(.out_width(4)) bit_extender_1 (.in(update), .out(bit_extender_1_out));
  Comparator comparator_1 (.a(counter_1_q), .b(8'h6), .eq(comparator_1_eq));  // open: gt, lt
  and and_2 (and_2_out, n0, n1, n2);
  and and_3 (and_3_out, n3, n4, n5);
  and and_4 (and_4_out, n6, n7, n8);
  and and_5 (and_5_out, n0, n3, n6);
  and and_6 (and_6_out, n1, n4, n7);
  and and_7 (and_7_out, n2, n5, n8);
  and and_8 (and_8_out, n0, n4, n8);
  and and_9 (and_9_out, n2, n4, n6);
  or or_1 (_1, controlled_buffer_1_out, demultiplexer_1_out0);
  or or_2 (_2, controlled_buffer_2_out, demultiplexer_1_out1);
  or or_3 (_3, controlled_buffer_3_out, demultiplexer_1_out2);
  or or_4 (_4, controlled_buffer_4_out, demultiplexer_1_out3);
  or or_5 (_5, controlled_buffer_5_out, demultiplexer_1_out4);
  or or_6 (_6, controlled_buffer_6_out, demultiplexer_1_out5);
  or or_7 (_7, controlled_buffer_7_out, demultiplexer_1_out6);
  or or_8 (_8, controlled_buffer_8_out, demultiplexer_1_out7);
  or or_9 (_9, pull_resistor_9_node, demultiplexer_1_out8);
  Demultiplexer #(.enable("false")) demultiplexer_2 (
    .out0(demultiplexer_2_out0), .out1(demultiplexer_2_out1), .in(_1), .sel(odd_parity_1_out));
  Demultiplexer #(.enable("false")) demultiplexer_3 (
    .out0(demultiplexer_3_out0), .out1(demultiplexer_3_out1), .in(_4), .sel(odd_parity_1_out));
  Demultiplexer #(.enable("false")) demultiplexer_4 (
    .out0(demultiplexer_4_out0), .out1(demultiplexer_4_out1), .in(_7), .sel(odd_parity_1_out));
  or or_10 (out_28, and_2_out, and_3_out, and_4_out, and_5_out, and_6_out, and_7_out, and_8_out, and_9_out);
  video video_1 (
    .\крестик (demultiplexer_2_out0), .\нолик (demultiplexer_2_out1), .reboot(reboot), .out_4(out_13),
    .out_5(out_14), .out_6(out_15), .out_7(out_16), .out_8(out_17), .\кнопка_горит (\video_1_кнопка_горит ),
    .\нолик_2 (n0), .\крестик_2 (v0));
  video video_2 (
    .\крестик (demultiplexer_3_out0), .\нолик (demultiplexer_3_out1), .reboot(reboot), .out_4(out_29),
    .out_5(out_30), .out_6(out_31), .out_7(out_32), .out_8(out_33), .\кнопка_горит (\video_2_кнопка_горит ),
    .\нолик_2 (n3), .\крестик_2 (v3));
  video video_3 (
    .\крестик (demultiplexer_4_out0), .\нолик (demultiplexer_4_out1), .reboot(reboot), .out_4(out_44),
    .out_5(out_45), .out_6(out_46), .out_7(out_47), .out_8(out_48), .\кнопка_горит (\video_3_кнопка_горит ),
    .\нолик_2 (n6), .\крестик_2 (v6));
  video video_4 (
    .\крестик (demultiplexer_5_out0), .\нолик (demultiplexer_5_out1), .reboot(reboot), .out_4(out_18),
    .out_5(out_19), .out_6(out_20), .out_7(out_21), .out_8(out_22), .\кнопка_горит (\video_4_кнопка_горит ),
    .\нолик_2 (n1), .\крестик_2 (v1));
  Demultiplexer #(.enable("false")) demultiplexer_5 (
    .out0(demultiplexer_5_out0), .out1(demultiplexer_5_out1), .in(_2), .sel(odd_parity_1_out));
  video video_5 (
    .\крестик (demultiplexer_6_out0), .\нолик (demultiplexer_6_out1), .reboot(reboot), .out_4(out_34),
    .out_5(out_35), .out_6(out_36), .out_7(out_37), .out_8(out_38), .\кнопка_горит (\video_5_кнопка_горит ),
    .\нолик_2 (n4), .\крестик_2 (v4));
  Demultiplexer #(.enable("false")) demultiplexer_6 (
    .out0(demultiplexer_6_out0), .out1(demultiplexer_6_out1), .in(_5), .sel(odd_parity_1_out));
  video video_6 (
    .\крестик (demultiplexer_7_out0), .\нолик (demultiplexer_7_out1), .reboot(reboot), .out_4(out_49),
    .out_5(out_50), .out_6(out_51), .out_7(out_52), .out_8(out_53), .\кнопка_горит (\video_6_кнопка_горит ),
    .\нолик_2 (n7), .\крестик_2 (v7));
  Demultiplexer #(.enable("false")) demultiplexer_7 (
    .out0(demultiplexer_7_out0), .out1(demultiplexer_7_out1), .in(_8), .sel(odd_parity_1_out));
  xor odd_parity_1 (odd_parity_1_out, \video_1_кнопка_горит , \video_2_кнопка_горит , \video_3_кнопка_горит , \video_4_кнопка_горит , \video_5_кнопка_горит , \video_6_кнопка_горит , \video_7_кнопка_горит , \video_8_кнопка_горит , \video_9_кнопка_горит );
  Demultiplexer #(.enable("false")) demultiplexer_8 (
    .out0(demultiplexer_8_out0), .out1(demultiplexer_8_out1), .in(_3), .sel(odd_parity_1_out));
  Demultiplexer #(.enable("false")) demultiplexer_9 (
    .out0(demultiplexer_9_out0), .out1(demultiplexer_9_out1), .in(_6), .sel(odd_parity_1_out));
  Demultiplexer #(.enable("false")) demultiplexer_10 (
    .out0(demultiplexer_10_out0), .out1(demultiplexer_10_out1), .in(_9), .sel(odd_parity_1_out));
  and and_10 (out_12, ~\крестик_win , ~out_28, \video_9_кнопка_горит , \video_8_кнопка_горит , \video_7_кнопка_горит , \video_6_кнопка_горит , \video_5_кнопка_горит , \video_4_кнопка_горит , \video_3_кнопка_горит , \video_2_кнопка_горит , \video_1_кнопка_горит );  // AND_Gate
  video video_7 (
    .\крестик (demultiplexer_8_out0), .\нолик (demultiplexer_8_out1), .reboot(reboot), .out_4(out_23),
    .out_5(out_24), .out_6(out_25), .out_7(out_26), .out_8(out_27), .\кнопка_горит (\video_7_кнопка_горит ),
    .\нолик_2 (n2), .\крестик_2 (v2));
  video video_8 (
    .\крестик (demultiplexer_9_out0), .\нолик (demultiplexer_9_out1), .reboot(reboot), .out_4(out_39),
    .out_5(out_40), .out_6(out_41), .out_7(out_42), .out_8(out_43), .\кнопка_горит (\video_8_кнопка_горит ),
    .\нолик_2 (n5), .\крестик_2 (v5));
  video video_9 (
    .\крестик (demultiplexer_10_out0), .\нолик (demultiplexer_10_out1), .reboot(reboot), .out_4(out_54),
    .out_5(out_55), .out_6(out_56), .out_7(out_57), .out_8(out_58), .\кнопка_горит (\video_9_кнопка_горит ),
    .\нолик_2 (n8), .\крестик_2 (v8));
  and and_11 (and_11_out, v0, v1, v2);
  and and_12 (and_12_out, v3, v4, v5);
  and and_13 (and_13_out, v6, v7, v8);
  and and_14 (and_14_out, v0, v3, v6);
  and and_15 (and_15_out, v1, v4, v7);
  and and_16 (and_16_out, v2, v5, v8);
  and and_17 (and_17_out, v0, v4, v8);
  and and_18 (and_18_out, v2, v4, v6);
  assign bit_extender_2_out = {{4{1'b0}}, priority_encoder_1_out};  // Bit_Extender bit_extender_2
  Priority_Encoder #(.select(4)) priority_encoder_1 (
    .in0(controlled_buffer_1_out), .in1(controlled_buffer_2_out), .in2(controlled_buffer_3_out),
    .in3(controlled_buffer_4_out), .in4(controlled_buffer_5_out), .in5(controlled_buffer_6_out),
    .in6(controlled_buffer_7_out), .in7(controlled_buffer_8_out), .in8(pull_resistor_9_node),
    .out(priority_encoder_1_out), .gs(priority_encoder_1_gs));  // open: in9, in10, in11, in12, in13, in14, in15, en_out, en_in
  or or_11 (or_11_out, out_12, out_28, not_2_out, proc_1_process, \крестик_win );
  or or_12 (\крестик_win , and_11_out, and_12_out, and_13_out, and_14_out, and_15_out, and_16_out, and_17_out, and_18_out);
  not not_2 (not_2_out, in_11);
  or or_13 (or_13_out, reboot, out_28, \крестик_win );
  Pull_Resistor pull_resistor_11 (.node(priority_encoder_1_gs));
  proc proc_1 (
    .in(bit_extender_2_out), .in_2(priority_encoder_1_gs), .clr(or_13_out), .process(proc_1_process),
    .out_4(up), .out(update));

  // Other names for the same wires on the sheet: clr = reboot; lose = \крестик_win ; win = out_28
endmodule

module proc (
  input  clr,
  input  [7:0] in,
  input  in_2,
  output out_4,
  output [7:0] out,
  output process
);

  wire and_1_out, and_4_out, cdm_8_mark5_1_data_inst, cdm_8_mark5_1_mem_cycle, clk, clock_1_out, clock_2_out,
       code, comparator_1_eq, data, I_O_addr, I_O_rw, I_O_sel, nand_1_out, not_1_out, not_2_out, not_3_out,
       or_1_out, or_2_out, or_3_out, r, RAM, register_4_q, up1, up2, w, xor_1_out;
  wire [7:0] addr, cdm_8_mark5_1_data_out, cdm_8_mark5_1_pc, cdm_8_mark5_1_ps, cdm_8_mark5_1_r0,
       cdm_8_mark5_1_r1, cdm_8_mark5_1_r2, cdm_8_mark5_1_r3, cdm_8_mark5_1_sp, controlled_buffer_2_out,
       counter_1_q, dat, demultiplexer_1_out1, register_2_q;

  not not_1 (not_1_out, or_1_out);
  Register #(.width(1)) register_1 (.D(in_2), .en(not_1_out), .Q(process), .clk(in_2), .clr(or_1_out));
  Clock clock_1 (.out(clock_1_out));
  assign clk = process ? clock_1_out : 1'bz;  // Controlled_Buffer controlled_buffer_1
  Pull_Resistor pull_resistor_1 (.node(clk));
  // Probe on cdm_8_mark5_1_r1
  // Probe on cdm_8_mark5_1_r3
  // Probe on cdm_8_mark5_1_r2
  // Probe on cdm_8_mark5_1_pc
  // Probe on cdm_8_mark5_1_r0
  or or_1 (or_1_out, and_1_out, clr);
  and and_1 (and_1_out, up2, clk);
  // Probe on cdm_8_mark5_1_ps
  // Probe on cdm_8_mark5_1_sp
  Decoder #(.disabled(0)) decoder_1 (
    .out0(code), .out1(data), .sel(cdm_8_mark5_1_data_inst), .en(cdm_8_mark5_1_mem_cycle));
  CdM_8_mark5 cdm_8_mark5_1 (
    .clock(clk), .addr(addr), .mem_read(I_O_rw), .mem_cycle(cdm_8_mark5_1_mem_cycle),
    .data_inst(cdm_8_mark5_1_data_inst), .data_out(cdm_8_mark5_1_data_out),
    .data_in(controlled_buffer_2_out), .r0(cdm_8_mark5_1_r0), .r1(cdm_8_mark5_1_r1), .r2(cdm_8_mark5_1_r2),
    .r3(cdm_8_mark5_1_r3), .PC(cdm_8_mark5_1_pc), .SP(cdm_8_mark5_1_sp), .PS(cdm_8_mark5_1_ps), .clr(or_1_out));  // open: IAck, IRQ, vec
  assign controlled_buffer_2_out = I_O_rw ? dat : 8'bz;  // Controlled_Buffer controlled_buffer_2
  Demultiplexer #(.width(8)) demultiplexer_1 (.out0(in), .out1(demultiplexer_1_out1), .in(dat), .sel(I_O_addr), .en(r));
  // Probe on addr
  not not_2 (not_2_out, I_O_rw);
  assign dat = not_2_out ? cdm_8_mark5_1_data_out : 8'bz;  // Controlled_Buffer controlled_buffer_3
  Register register_2 (.D(in), .en(in_2), .Q(register_2_q), .clk(clk), .clr(clr));
  // Probe on dat
  RAM ram_1 (.addr(addr), .data(dat), .sel(RAM), .clk(clk), .ld(I_O_rw), .clr(clr));
  ROM rom_1 (.addr(addr), .data(dat), .sel(code));
  Register register_3 (.D(demultiplexer_1_out1), .en(up2), .Q(out), .clk(clk), .clr(clr));
  Pull_Resistor pull_resistor_2 (.node(clr));
  and and_2 (I_O_sel, not_3_out, data);
  Multiplexer #(.width(8)) multiplexer_1 (.in0(register_2_q), .in1(out), .out(dat), .sel(I_O_addr), .en(w));
  Decoder #(.disabled(0)) decoder_2 (.out0(up1), .out1(up2), .sel(I_O_addr), .en(r));
  not not_3 (not_3_out, nand_1_out);
  and and_3 (RAM, nand_1_out, data);
  nand nand_1 (nand_1_out, xor_1_out, ~addr[2], addr[3], addr[4], addr[5], addr[6], addr[7]);  // NAND_Gate
  // Priority_Encoder #(.select(1), .disabled(0)) priority_encoder_1: pin names not known; wires that end beside it: I_O_addr, addr[0], addr[1]
  xor xor_1 (xor_1_out, addr[0], addr[1]);
  Decoder #(.disabled(0)) decoder_3 (.out0(r), .out1(w), .sel(I_O_rw), .en(I_O_sel));
  Register #(.width(1)) register_4 (.D(up2), .en(up2), .Q(register_4_q), .clk(up2), .clr(or_2_out));
  or or_2 (or_2_out, in_2, comparator_1_eq, clr);
  Clock clock_2 (.out(clock_2_out));
  and and_4 (and_4_out, register_4_q, clock_2_out);
  Counter counter_1 (.Q(counter_1_q), .clk(and_4_out), .clr(comparator_1_eq));  // open: load, D, count, carry
  or or_3 (or_3_out, in_2, clr);
  Register #(.width(1)) register_5 (
    .D(register_4_q), .en(comparator_1_eq), .Q(out_4), .clk(comparator_1_eq), .clr(or_3_out));
  Comparator comparator_1 (.a(counter_1_q), .b(8'h4), .eq(comparator_1_eq));  // open: gt, lt

  // Other names for the same wires on the sheet: button = in_2; I_O_data[7:0] = dat; rw = I_O_rw

  // Notes on the sheet:
  //   contents of rom_1 (hex, n*v repeats v):
  //   0 1 2 3 4 5 6 7 8 0 3 6 1 4 7 2 5 8 0 4 8 2 4 6 d0 0 d1 18 f2 a2 8c 89 e1 1c d0 f9 b0 d1 f0 14 b2 a
  //   e1 31 d2 3 a2 ee 33 ee c6 d0 f4 b1 5 e1 3e d2 1 a2 ee c6 d0 0 d1 18 d3 0 c1 d2 f0 b1 16 b9 17 8c d2
  //   f0 b1 16 b9 17 8c d2 f0 b1 16 b9 17 8c c0 d0 9 7c e1 64 c4 c5 ee c6 d0 6 7c e0 6e d0 2 7c e1 a3 c4
  //   c5 88 c0 b0 d2 f0 12 c4 b9 5 e1 81 d1 1 a9 8 ee c6 88 c0 b0 d2 f0 12 c4 b9 5 e1 92 d1 1 a9 8 ee c6
  //   88 c0 b0 d2 f0 12 c4 b9 5 e1 a3 d1 1 a9 8 ee c6 d2 3 c4 c5 39 85 e1 42 d0 f0 d2 f9 72 e1 b4 ee c6 b1
  //   5 e1 c3 d2 1 a2 d1 f0 34 84 ee c6 ee c6 8c ee ad d3 fa ac d4
  //   read
  //   write
endmodule
